// Logisim project pj1_new.circ as structural Verilog: 20 circuits, main circuit TOP_LEVEL
// EX/MEM
module TOP_LEVEL (
);

  wire clock_1_out, Comparator_branch, CtrlUnit_alubsrc, CtrlUnit_halt, CtrlUnit_led, CtrlUnit_memread,
       CtrlUnit_memtoreg, CtrlUnit_memwrite, CtrlUnit_regwrite, display_displaysignalgenerator_1_o_immd_neg,
       display_displaysignalgenerator_2_o_immd_neg, display_displaysignalgenerator_3_o_immd_neg,
       display_displaysignalgenerator_4_o_immd_neg, display_displaysignalgenerator_5_o_immd_neg,
       display_registerviewer_1_o_immd_neg, display_registerviewer_2_o_immd_neg,
       display_registerviewer_3_o_immd_neg, display_registerviewer_4_o_immd_neg,
       display_registerviewer_5_o_immd_neg, display_registerviewer_6_o_immd_neg,
       display_registerviewer_7_o_immd_neg, display_registerviewer_8_o_immd_neg,
       display_registerviewer_9_o_immd_neg, display_registerviewer_10_o_immd_neg,
       display_registerviewer_11_o_immd_neg, EX_MEM_controlunitrelated_7, EX_MEM_controlunitrelated_8,
       EX_MEM_controlunitrelated_9, EX_MEM_controlunitrelated_10, EX_MEM_controlunitrelated_11,
       EX_MEM_controlunitrelated_12, ID_EX_controlunitrelated_8, ID_EX_controlunitrelated_9,
       ID_EX_controlunitrelated_10, ID_EX_controlunitrelated_11, ID_EX_controlunitrelated_12,
       ID_EX_controlunitrelated_13, ID_EX_controlunitrelated_14, MEM_WB_controlunitrelated_4,
       MEM_WB_controlunitrelated_5, MEM_WB_controlunitrelated_6, new_halt_1_latch_wrt, new_halt_1_pc_enable,
       new_input_1_clear, new_input_1_clk_2, new_nop_1_regwrite_2, not_1_out, SmartSplitter_unsigned;
  wire [2:0] EX_MEM_rs_2, EX_MEM_rt_2, ID_EX_rs_2, ID_EX_rt_2, MEM_WB_rs_2, SmartSplitter_rs,
       SmartSplitter_rt;
  wire [3:0] display_displaysignalgenerator_1_o_immd_dig, display_displaysignalgenerator_1_o_immd_dig_1,
       display_displaysignalgenerator_1_o_immd_dig_2, display_displaysignalgenerator_1_o_immd_dig_3,
       display_displaysignalgenerator_1_o_immd_dig_4, display_displaysignalgenerator_1_o_rs1_dig,
       display_displaysignalgenerator_1_o_rs1_dig_1, display_displaysignalgenerator_1_o_rs2_dig,
       display_displaysignalgenerator_1_o_rs2_dig_1, display_displaysignalgenerator_2_o_immd_dig,
       display_displaysignalgenerator_2_o_immd_dig_1, display_displaysignalgenerator_2_o_immd_dig_2,
       display_displaysignalgenerator_2_o_immd_dig_3, display_displaysignalgenerator_2_o_immd_dig_4,
       display_displaysignalgenerator_2_o_rs1_dig, display_displaysignalgenerator_2_o_rs1_dig_1,
       display_displaysignalgenerator_2_o_rs2_dig, display_displaysignalgenerator_2_o_rs2_dig_1,
       display_displaysignalgenerator_3_o_immd_dig, display_displaysignalgenerator_3_o_immd_dig_1,
       display_displaysignalgenerator_3_o_immd_dig_2, display_displaysignalgenerator_3_o_immd_dig_3,
       display_displaysignalgenerator_3_o_immd_dig_4, display_displaysignalgenerator_3_o_rs1_dig,
       display_displaysignalgenerator_3_o_rs1_dig_1, display_displaysignalgenerator_3_o_rs2_dig,
       display_displaysignalgenerator_3_o_rs2_dig_1, display_displaysignalgenerator_4_o_immd_dig,
       display_displaysignalgenerator_4_o_immd_dig_1, display_displaysignalgenerator_4_o_immd_dig_2,
       display_displaysignalgenerator_4_o_immd_dig_3, display_displaysignalgenerator_4_o_immd_dig_4,
       display_displaysignalgenerator_4_o_rs1_dig, display_displaysignalgenerator_4_o_rs1_dig_1,
       display_displaysignalgenerator_4_o_rs2_dig, display_displaysignalgenerator_4_o_rs2_dig_1,
       display_displaysignalgenerator_5_o_immd_dig, display_displaysignalgenerator_5_o_immd_dig_1,
       display_displaysignalgenerator_5_o_immd_dig_2, display_displaysignalgenerator_5_o_immd_dig_3,
       display_displaysignalgenerator_5_o_immd_dig_4, display_displaysignalgenerator_5_o_rs1_dig,
       display_displaysignalgenerator_5_o_rs1_dig_1, display_displaysignalgenerator_5_o_rs2_dig,
       display_displaysignalgenerator_5_o_rs2_dig_1, display_registerviewer_1_o_immd_dig,
       display_registerviewer_1_o_immd_dig_1, display_registerviewer_1_o_immd_dig_2,
       display_registerviewer_1_o_immd_dig_3, display_registerviewer_1_o_immd_dig_4,
       display_registerviewer_2_o_immd_dig, display_registerviewer_2_o_immd_dig_1,
       display_registerviewer_2_o_immd_dig_2, display_registerviewer_2_o_immd_dig_3,
       display_registerviewer_2_o_immd_dig_4, display_registerviewer_3_o_immd_dig,
       display_registerviewer_3_o_immd_dig_1, display_registerviewer_3_o_immd_dig_2,
       display_registerviewer_3_o_immd_dig_3, display_registerviewer_3_o_immd_dig_4,
       display_registerviewer_4_o_immd_dig, display_registerviewer_4_o_immd_dig_1,
       display_registerviewer_4_o_immd_dig_2, display_registerviewer_4_o_immd_dig_3,
       display_registerviewer_4_o_immd_dig_4, display_registerviewer_5_o_immd_dig,
       display_registerviewer_5_o_immd_dig_1, display_registerviewer_5_o_immd_dig_2,
       display_registerviewer_5_o_immd_dig_3, display_registerviewer_5_o_immd_dig_4,
       display_registerviewer_6_o_immd_dig, display_registerviewer_6_o_immd_dig_1,
       display_registerviewer_6_o_immd_dig_2, display_registerviewer_6_o_immd_dig_3,
       display_registerviewer_6_o_immd_dig_4, display_registerviewer_7_o_immd_dig,
       display_registerviewer_7_o_immd_dig_1, display_registerviewer_7_o_immd_dig_2,
       display_registerviewer_7_o_immd_dig_3, display_registerviewer_7_o_immd_dig_4,
       display_registerviewer_8_o_immd_dig, display_registerviewer_8_o_immd_dig_1,
       display_registerviewer_8_o_immd_dig_2, display_registerviewer_8_o_immd_dig_3,
       display_registerviewer_8_o_immd_dig_4, display_registerviewer_9_o_immd_dig,
       display_registerviewer_9_o_immd_dig_1, display_registerviewer_9_o_immd_dig_2,
       display_registerviewer_9_o_immd_dig_3, display_registerviewer_9_o_immd_dig_4,
       display_registerviewer_10_o_immd_dig, display_registerviewer_10_o_immd_dig_1,
       display_registerviewer_10_o_immd_dig_2, display_registerviewer_10_o_immd_dig_3,
       display_registerviewer_10_o_immd_dig_4, display_registerviewer_11_o_immd_dig,
       display_registerviewer_11_o_immd_dig_1, display_registerviewer_11_o_immd_dig_2,
       display_registerviewer_11_o_immd_dig_3, display_registerviewer_11_o_immd_dig_4, ID_EX_instrnum_2,
       SmartSplitter_instrnum;
  wire [6:0] keyboard_1_data;
  wire [7:0] adder_1_out, bit_extender_1_out, display_displaysignalgenerator_1_o_ins_mtx,
       display_displaysignalgenerator_1_o_ins_mtx_1, display_displaysignalgenerator_1_o_ins_mtx_2,
       display_displaysignalgenerator_1_o_ins_mtx_3, display_displaysignalgenerator_1_o_ins_mtx_4,
       display_displaysignalgenerator_1_o_ins_mtx_5, display_displaysignalgenerator_1_o_ins_mtx_6,
       display_displaysignalgenerator_1_o_ins_mtx_7, display_displaysignalgenerator_1_o_ins_mtx_8,
       display_displaysignalgenerator_1_o_ins_mtx_9, display_displaysignalgenerator_1_o_ins_mtx_10,
       display_displaysignalgenerator_1_o_ins_mtx_11, display_displaysignalgenerator_1_o_ins_mtx_12,
       display_displaysignalgenerator_1_o_ins_mtx_13, display_displaysignalgenerator_1_o_ins_mtx_14,
       display_displaysignalgenerator_1_o_ins_mtx_15, display_displaysignalgenerator_1_o_rs1_mtx,
       display_displaysignalgenerator_1_o_rs1_mtx_1, display_displaysignalgenerator_1_o_rs1_mtx_2,
       display_displaysignalgenerator_1_o_rs1_mtx_3, display_displaysignalgenerator_1_o_rs2_mtx,
       display_displaysignalgenerator_1_o_rs2_mtx_1, display_displaysignalgenerator_1_o_rs2_mtx_2,
       display_displaysignalgenerator_1_o_rs2_mtx_3, display_displaysignalgenerator_2_o_ins_mtx,
       display_displaysignalgenerator_2_o_ins_mtx_1, display_displaysignalgenerator_2_o_ins_mtx_2,
       display_displaysignalgenerator_2_o_ins_mtx_3, display_displaysignalgenerator_2_o_ins_mtx_4,
       display_displaysignalgenerator_2_o_ins_mtx_5, display_displaysignalgenerator_2_o_ins_mtx_6,
       display_displaysignalgenerator_2_o_ins_mtx_7, display_displaysignalgenerator_2_o_ins_mtx_8,
       display_displaysignalgenerator_2_o_ins_mtx_9, display_displaysignalgenerator_2_o_ins_mtx_10,
       display_displaysignalgenerator_2_o_ins_mtx_11, display_displaysignalgenerator_2_o_ins_mtx_12,
       display_displaysignalgenerator_2_o_ins_mtx_13, display_displaysignalgenerator_2_o_ins_mtx_14,
       display_displaysignalgenerator_2_o_ins_mtx_15, display_displaysignalgenerator_2_o_rs1_mtx,
       display_displaysignalgenerator_2_o_rs1_mtx_1, display_displaysignalgenerator_2_o_rs1_mtx_2,
       display_displaysignalgenerator_2_o_rs1_mtx_3, display_displaysignalgenerator_2_o_rs2_mtx,
       display_displaysignalgenerator_2_o_rs2_mtx_1, display_displaysignalgenerator_2_o_rs2_mtx_2,
       display_displaysignalgenerator_2_o_rs2_mtx_3, display_displaysignalgenerator_3_o_ins_mtx,
       display_displaysignalgenerator_3_o_ins_mtx_1, display_displaysignalgenerator_3_o_ins_mtx_2,
       display_displaysignalgenerator_3_o_ins_mtx_3, display_displaysignalgenerator_3_o_ins_mtx_4,
       display_displaysignalgenerator_3_o_ins_mtx_5, display_displaysignalgenerator_3_o_ins_mtx_6,
       display_displaysignalgenerator_3_o_ins_mtx_7, display_displaysignalgenerator_3_o_ins_mtx_8,
       display_displaysignalgenerator_3_o_ins_mtx_9, display_displaysignalgenerator_3_o_ins_mtx_10,
       display_displaysignalgenerator_3_o_ins_mtx_11, display_displaysignalgenerator_3_o_ins_mtx_12,
       display_displaysignalgenerator_3_o_ins_mtx_13, display_displaysignalgenerator_3_o_ins_mtx_14,
       display_displaysignalgenerator_3_o_ins_mtx_15, display_displaysignalgenerator_3_o_rs1_mtx,
       display_displaysignalgenerator_3_o_rs1_mtx_1, display_displaysignalgenerator_3_o_rs1_mtx_2,
       display_displaysignalgenerator_3_o_rs1_mtx_3, display_displaysignalgenerator_3_o_rs2_mtx,
       display_displaysignalgenerator_3_o_rs2_mtx_1, display_displaysignalgenerator_3_o_rs2_mtx_2,
       display_displaysignalgenerator_3_o_rs2_mtx_3, display_displaysignalgenerator_4_o_ins_mtx,
       display_displaysignalgenerator_4_o_ins_mtx_1, display_displaysignalgenerator_4_o_ins_mtx_2,
       display_displaysignalgenerator_4_o_ins_mtx_3, display_displaysignalgenerator_4_o_ins_mtx_4,
       display_displaysignalgenerator_4_o_ins_mtx_5, display_displaysignalgenerator_4_o_ins_mtx_6,
       display_displaysignalgenerator_4_o_ins_mtx_7, display_displaysignalgenerator_4_o_ins_mtx_8,
       display_displaysignalgenerator_4_o_ins_mtx_9, display_displaysignalgenerator_4_o_ins_mtx_10,
       display_displaysignalgenerator_4_o_ins_mtx_11, display_displaysignalgenerator_4_o_ins_mtx_12,
       display_displaysignalgenerator_4_o_ins_mtx_13, display_displaysignalgenerator_4_o_ins_mtx_14,
       display_displaysignalgenerator_4_o_ins_mtx_15, display_displaysignalgenerator_4_o_rs1_mtx,
       display_displaysignalgenerator_4_o_rs1_mtx_1, display_displaysignalgenerator_4_o_rs1_mtx_2,
       display_displaysignalgenerator_4_o_rs1_mtx_3, display_displaysignalgenerator_4_o_rs2_mtx,
       display_displaysignalgenerator_4_o_rs2_mtx_1, display_displaysignalgenerator_4_o_rs2_mtx_2,
       display_displaysignalgenerator_4_o_rs2_mtx_3, display_displaysignalgenerator_5_o_ins_mtx,
       display_displaysignalgenerator_5_o_ins_mtx_1, display_displaysignalgenerator_5_o_ins_mtx_2,
       display_displaysignalgenerator_5_o_ins_mtx_3, display_displaysignalgenerator_5_o_ins_mtx_4,
       display_displaysignalgenerator_5_o_ins_mtx_5, display_displaysignalgenerator_5_o_ins_mtx_6,
       display_displaysignalgenerator_5_o_ins_mtx_7, display_displaysignalgenerator_5_o_ins_mtx_8,
       display_displaysignalgenerator_5_o_ins_mtx_9, display_displaysignalgenerator_5_o_ins_mtx_10,
       display_displaysignalgenerator_5_o_ins_mtx_11, display_displaysignalgenerator_5_o_ins_mtx_12,
       display_displaysignalgenerator_5_o_ins_mtx_13, display_displaysignalgenerator_5_o_ins_mtx_14,
       display_displaysignalgenerator_5_o_ins_mtx_15, display_displaysignalgenerator_5_o_rs1_mtx,
       display_displaysignalgenerator_5_o_rs1_mtx_1, display_displaysignalgenerator_5_o_rs1_mtx_2,
       display_displaysignalgenerator_5_o_rs1_mtx_3, display_displaysignalgenerator_5_o_rs2_mtx,
       display_displaysignalgenerator_5_o_rs2_mtx_1, display_displaysignalgenerator_5_o_rs2_mtx_2,
       display_displaysignalgenerator_5_o_rs2_mtx_3, multiplexer_1_out, PC_q, SmartSplitter_immediate;
  wire [15:0] EX_MEM_aluout_2, EX_MEM_instruction_2, EX_MEM_readdata2_2, ForwardingA_Rs_readdata_2,
       ForwardingB_Rt_2_readdata_2, ForwardingB_Rt_readdata_2, hdu_cmux_1_writedata_2,
       hdu_forward_1_readdata_2, ID_EX_instruction_2, ID_EX_read1_2, ID_EX_read2_2, ID_EX_signextender_2,
       IF_ID_instuction_2, IF_ID_instuction_3, MEM_WB_aluout_2, MEM_WB_instruction_2, MEM_WB_readdata_2,
       multiplexer_2_out, multiplexer_3_out, new_alu_1_out, ram_1_data, register_2_q, Register_readdata1,
       Register_readdata2, Register_viewer, Register_viewer_2, Register_viewer_3, Register_viewer_4,
       Register_viewer_5, Register_viewer_6, Register_viewer_7, Register_viewer_8, rom_1_data,
       SignExtender_immextended;

  display_displaySignalGenerator display_displaysignalgenerator_1 (
    .o_rs2_mtx(display_displaysignalgenerator_1_o_rs2_mtx),
    .o_rs2_mtx_1(display_displaysignalgenerator_1_o_rs2_mtx_1),
    .o_rs2_mtx_2(display_displaysignalgenerator_1_o_rs2_mtx_2),
    .o_rs2_mtx_3(display_displaysignalgenerator_1_o_rs2_mtx_3),
    .o_rs2_dig(display_displaysignalgenerator_1_o_rs2_dig),
    .o_rs2_dig_1(display_displaysignalgenerator_1_o_rs2_dig_1),
    .o_ins_mtx(display_displaysignalgenerator_1_o_ins_mtx),
    .o_ins_mtx_1(display_displaysignalgenerator_1_o_ins_mtx_1),
    .o_ins_mtx_2(display_displaysignalgenerator_1_o_ins_mtx_2),
    .o_ins_mtx_3(display_displaysignalgenerator_1_o_ins_mtx_3),
    .o_ins_mtx_4(display_displaysignalgenerator_1_o_ins_mtx_4),
    .o_ins_mtx_5(display_displaysignalgenerator_1_o_ins_mtx_5),
    .o_ins_mtx_6(display_displaysignalgenerator_1_o_ins_mtx_6),
    .o_ins_mtx_7(display_displaysignalgenerator_1_o_ins_mtx_7),
    .o_ins_mtx_8(display_displaysignalgenerator_1_o_ins_mtx_8),
    .o_ins_mtx_9(display_displaysignalgenerator_1_o_ins_mtx_9),
    .o_ins_mtx_10(display_displaysignalgenerator_1_o_ins_mtx_10),
    .o_ins_mtx_11(display_displaysignalgenerator_1_o_ins_mtx_11),
    .o_ins_mtx_12(display_displaysignalgenerator_1_o_ins_mtx_12),
    .o_ins_mtx_13(display_displaysignalgenerator_1_o_ins_mtx_13),
    .o_ins_mtx_14(display_displaysignalgenerator_1_o_ins_mtx_14),
    .o_ins_mtx_15(display_displaysignalgenerator_1_o_ins_mtx_15),
    .o_rs1_mtx(display_displaysignalgenerator_1_o_rs1_mtx),
    .o_rs1_mtx_1(display_displaysignalgenerator_1_o_rs1_mtx_1),
    .o_rs1_mtx_2(display_displaysignalgenerator_1_o_rs1_mtx_2),
    .o_rs1_mtx_3(display_displaysignalgenerator_1_o_rs1_mtx_3),
    .o_rs1_dig(display_displaysignalgenerator_1_o_rs1_dig),
    .o_rs1_dig_1(display_displaysignalgenerator_1_o_rs1_dig_1), .i_inst(rom_1_data),
    .o_immd_neg(display_displaysignalgenerator_1_o_immd_neg),
    .o_immd_dig(display_displaysignalgenerator_1_o_immd_dig),
    .o_immd_dig_1(display_displaysignalgenerator_1_o_immd_dig_1),
    .o_immd_dig_2(display_displaysignalgenerator_1_o_immd_dig_2),
    .o_immd_dig_3(display_displaysignalgenerator_1_o_immd_dig_3),
    .o_immd_dig_4(display_displaysignalgenerator_1_o_immd_dig_4));
  DotMatrix #(.matrixcols(4), .matrixrows(8)) dotmatrix_1 (
    .col0(display_displaysignalgenerator_1_o_ins_mtx_4), .col1(display_displaysignalgenerator_1_o_ins_mtx_5),
    .col2(display_displaysignalgenerator_1_o_ins_mtx_6), .col3(display_displaysignalgenerator_1_o_ins_mtx_7));
  DotMatrix #(.matrixcols(4), .matrixrows(8)) dotmatrix_2 (
    .col0(display_displaysignalgenerator_1_o_ins_mtx), .col1(display_displaysignalgenerator_1_o_ins_mtx_1),
    .col2(display_displaysignalgenerator_1_o_ins_mtx_2), .col3(display_displaysignalgenerator_1_o_ins_mtx_3));
  Hex_Digit_Display hex_digit_display_1 (.value(register_2_q[15:12]));  // open: dp
  _7_Segment_Display u_7_segment_display_1 (.g(display_registerviewer_1_o_immd_neg));  // open: f, a, b, e, d, c, dp
  _7_Segment_Display u_7_segment_display_2 (.g(display_registerviewer_2_o_immd_neg));  // open: f, a, b, e, d, c, dp
  _7_Segment_Display u_7_segment_display_3 (.g(display_registerviewer_3_o_immd_neg));  // open: f, a, b, e, d, c, dp
  _7_Segment_Display u_7_segment_display_4 (.g(display_registerviewer_4_o_immd_neg));  // open: f, a, b, e, d, c, dp
  _7_Segment_Display u_7_segment_display_5 (.g(display_registerviewer_5_o_immd_neg));  // open: f, a, b, e, d, c, dp
  _7_Segment_Display u_7_segment_display_6 (.g(display_registerviewer_6_o_immd_neg));  // open: f, a, b, e, d, c, dp
  _7_Segment_Display u_7_segment_display_7 (.g(display_registerviewer_7_o_immd_neg));  // open: f, a, b, e, d, c, dp
  _7_Segment_Display u_7_segment_display_8 (.g(display_registerviewer_8_o_immd_neg));  // open: f, a, b, e, d, c, dp
  DotMatrix #(.matrixcols(4), .matrixrows(8)) dotmatrix_3 (
    .col0(display_displaysignalgenerator_1_o_ins_mtx_8), .col1(display_displaysignalgenerator_1_o_ins_mtx_9),
    .col2(display_displaysignalgenerator_1_o_ins_mtx_10), .col3(display_displaysignalgenerator_1_o_ins_mtx_11));
  DotMatrix #(.matrixcols(4), .matrixrows(8)) dotmatrix_4 (
    .col0(display_displaysignalgenerator_1_o_ins_mtx_12),
    .col1(display_displaysignalgenerator_1_o_ins_mtx_13),
    .col2(display_displaysignalgenerator_1_o_ins_mtx_14), .col3(display_displaysignalgenerator_1_o_ins_mtx_15));
  Hex_Digit_Display hex_digit_display_2 (.value(register_2_q[11:8]));  // open: dp
  Hex_Digit_Display hex_digit_display_3 (.value(register_2_q[7:4]));  // open: dp
  Hex_Digit_Display hex_digit_display_4 (.value(display_registerviewer_1_o_immd_dig));  // open: dp
  Hex_Digit_Display hex_digit_display_5 (.value(display_registerviewer_1_o_immd_dig_1));  // open: dp
  Hex_Digit_Display hex_digit_display_6 (.value(display_registerviewer_2_o_immd_dig));  // open: dp
  Hex_Digit_Display hex_digit_display_7 (.value(display_registerviewer_2_o_immd_dig_1));  // open: dp
  Hex_Digit_Display hex_digit_display_8 (.value(display_registerviewer_3_o_immd_dig_1));  // open: dp
  Hex_Digit_Display hex_digit_display_9 (.value(display_registerviewer_3_o_immd_dig));  // open: dp
  Hex_Digit_Display hex_digit_display_10 (.value(display_registerviewer_4_o_immd_dig));  // open: dp
  Hex_Digit_Display hex_digit_display_11 (.value(display_registerviewer_4_o_immd_dig_1));  // open: dp
  Hex_Digit_Display hex_digit_display_12 (.value(display_registerviewer_5_o_immd_dig));  // open: dp
  Hex_Digit_Display hex_digit_display_13 (.value(display_registerviewer_5_o_immd_dig_1));  // open: dp
  Hex_Digit_Display hex_digit_display_14 (.value(display_registerviewer_6_o_immd_dig));  // open: dp
  Hex_Digit_Display hex_digit_display_15 (.value(display_registerviewer_6_o_immd_dig_1));  // open: dp
  Hex_Digit_Display hex_digit_display_16 (.value(display_registerviewer_7_o_immd_dig));  // open: dp
  Hex_Digit_Display hex_digit_display_17 (.value(display_registerviewer_7_o_immd_dig_1));  // open: dp
  Hex_Digit_Display hex_digit_display_18 (.value(display_registerviewer_8_o_immd_dig));  // open: dp
  Hex_Digit_Display hex_digit_display_19 (.value(display_registerviewer_8_o_immd_dig_1));  // open: dp
  DotMatrix #(.matrixcols(4), .matrixrows(8)) dotmatrix_5 (
    .col0(display_displaysignalgenerator_1_o_rs1_mtx), .col1(display_displaysignalgenerator_1_o_rs1_mtx_1),
    .col2(display_displaysignalgenerator_1_o_rs1_mtx_2), .col3(display_displaysignalgenerator_1_o_rs1_mtx_3));
  Hex_Digit_Display hex_digit_display_20 (.value(register_2_q[3:0]));  // open: dp
  Hex_Digit_Display hex_digit_display_21 (.value(display_registerviewer_1_o_immd_dig_3));  // open: dp
  Hex_Digit_Display hex_digit_display_22 (.value(display_registerviewer_1_o_immd_dig_2));  // open: dp
  Hex_Digit_Display hex_digit_display_23 (.value(display_registerviewer_2_o_immd_dig_2));  // open: dp
  Hex_Digit_Display hex_digit_display_24 (.value(display_registerviewer_2_o_immd_dig_3));  // open: dp
  Hex_Digit_Display hex_digit_display_25 (.value(display_registerviewer_3_o_immd_dig_2));  // open: dp
  Hex_Digit_Display hex_digit_display_26 (.value(display_registerviewer_3_o_immd_dig_3));  // open: dp
  Hex_Digit_Display hex_digit_display_27 (.value(display_registerviewer_4_o_immd_dig_3));  // open: dp
  Hex_Digit_Display hex_digit_display_28 (.value(display_registerviewer_4_o_immd_dig_2));  // open: dp
  Hex_Digit_Display hex_digit_display_29 (.value(display_registerviewer_5_o_immd_dig_2));  // open: dp
  Hex_Digit_Display hex_digit_display_30 (.value(display_registerviewer_5_o_immd_dig_3));  // open: dp
  Hex_Digit_Display hex_digit_display_31 (.value(display_registerviewer_6_o_immd_dig_3));  // open: dp
  Hex_Digit_Display hex_digit_display_32 (.value(display_registerviewer_6_o_immd_dig_2));  // open: dp
  Hex_Digit_Display hex_digit_display_33 (.value(display_registerviewer_7_o_immd_dig_3));  // open: dp
  Hex_Digit_Display hex_digit_display_34 (.value(display_registerviewer_7_o_immd_dig_2));  // open: dp
  Hex_Digit_Display hex_digit_display_35 (.value(display_registerviewer_8_o_immd_dig_3));  // open: dp
  Hex_Digit_Display hex_digit_display_36 (.value(display_registerviewer_8_o_immd_dig_2));  // open: dp
  Hex_Digit_Display hex_digit_display_37 (.value(display_displaysignalgenerator_1_o_rs1_dig_1));  // open: dp
  Hex_Digit_Display hex_digit_display_38 (.value(display_displaysignalgenerator_1_o_rs1_dig));  // open: dp
  DotMatrix #(.matrixcols(4), .matrixrows(8)) dotmatrix_6 (
    .col0(display_displaysignalgenerator_1_o_rs2_mtx), .col1(display_displaysignalgenerator_1_o_rs2_mtx_1),
    .col2(display_displaysignalgenerator_1_o_rs2_mtx_2), .col3(display_displaysignalgenerator_1_o_rs2_mtx_3));
  LED Halt (.in(MEM_WB_controlunitrelated_6));
  display_registerViewer display_registerviewer_1 (
    .in_1(Register_viewer), .o_immd_neg(display_registerviewer_1_o_immd_neg),
    .o_immd_dig(display_registerviewer_1_o_immd_dig), .o_immd_dig_1(display_registerviewer_1_o_immd_dig_1),
    .o_immd_dig_2(display_registerviewer_1_o_immd_dig_2),
    .o_immd_dig_3(display_registerviewer_1_o_immd_dig_3), .o_immd_dig_4(display_registerviewer_1_o_immd_dig_4));
  Hex_Digit_Display hex_digit_display_39 (.value(display_registerviewer_1_o_immd_dig_4));  // open: dp
  display_registerViewer display_registerviewer_2 (
    .in_1(Register_viewer_2), .o_immd_neg(display_registerviewer_2_o_immd_neg),
    .o_immd_dig(display_registerviewer_2_o_immd_dig), .o_immd_dig_1(display_registerviewer_2_o_immd_dig_1),
    .o_immd_dig_2(display_registerviewer_2_o_immd_dig_2),
    .o_immd_dig_3(display_registerviewer_2_o_immd_dig_3), .o_immd_dig_4(display_registerviewer_2_o_immd_dig_4));
  Hex_Digit_Display hex_digit_display_40 (.value(display_registerviewer_2_o_immd_dig_4));  // open: dp
  display_registerViewer display_registerviewer_3 (
    .in_1(Register_viewer_3), .o_immd_neg(display_registerviewer_3_o_immd_neg),
    .o_immd_dig(display_registerviewer_3_o_immd_dig), .o_immd_dig_1(display_registerviewer_3_o_immd_dig_1),
    .o_immd_dig_2(display_registerviewer_3_o_immd_dig_2),
    .o_immd_dig_3(display_registerviewer_3_o_immd_dig_3), .o_immd_dig_4(display_registerviewer_3_o_immd_dig_4));
  Hex_Digit_Display hex_digit_display_41 (.value(display_registerviewer_3_o_immd_dig_4));  // open: dp
  display_registerViewer display_registerviewer_4 (
    .in_1(Register_viewer_4), .o_immd_neg(display_registerviewer_4_o_immd_neg),
    .o_immd_dig(display_registerviewer_4_o_immd_dig), .o_immd_dig_1(display_registerviewer_4_o_immd_dig_1),
    .o_immd_dig_2(display_registerviewer_4_o_immd_dig_2),
    .o_immd_dig_3(display_registerviewer_4_o_immd_dig_3), .o_immd_dig_4(display_registerviewer_4_o_immd_dig_4));
  Hex_Digit_Display hex_digit_display_42 (.value(display_registerviewer_4_o_immd_dig_4));  // open: dp
  display_registerViewer display_registerviewer_5 (
    .in_1(Register_viewer_5), .o_immd_neg(display_registerviewer_5_o_immd_neg),
    .o_immd_dig(display_registerviewer_5_o_immd_dig), .o_immd_dig_1(display_registerviewer_5_o_immd_dig_1),
    .o_immd_dig_2(display_registerviewer_5_o_immd_dig_2),
    .o_immd_dig_3(display_registerviewer_5_o_immd_dig_3), .o_immd_dig_4(display_registerviewer_5_o_immd_dig_4));
  Hex_Digit_Display hex_digit_display_43 (.value(display_registerviewer_5_o_immd_dig_4));  // open: dp
  display_registerViewer display_registerviewer_6 (
    .in_1(Register_viewer_6), .o_immd_neg(display_registerviewer_6_o_immd_neg),
    .o_immd_dig(display_registerviewer_6_o_immd_dig), .o_immd_dig_1(display_registerviewer_6_o_immd_dig_1),
    .o_immd_dig_2(display_registerviewer_6_o_immd_dig_2),
    .o_immd_dig_3(display_registerviewer_6_o_immd_dig_3), .o_immd_dig_4(display_registerviewer_6_o_immd_dig_4));
  Hex_Digit_Display hex_digit_display_44 (.value(display_registerviewer_6_o_immd_dig_4));  // open: dp
  display_registerViewer display_registerviewer_7 (
    .in_1(Register_viewer_7), .o_immd_neg(display_registerviewer_7_o_immd_neg),
    .o_immd_dig(display_registerviewer_7_o_immd_dig), .o_immd_dig_1(display_registerviewer_7_o_immd_dig_1),
    .o_immd_dig_2(display_registerviewer_7_o_immd_dig_2),
    .o_immd_dig_3(display_registerviewer_7_o_immd_dig_3), .o_immd_dig_4(display_registerviewer_7_o_immd_dig_4));
  Hex_Digit_Display hex_digit_display_45 (.value(display_registerviewer_7_o_immd_dig_4));  // open: dp
  display_registerViewer display_registerviewer_8 (
    .in_1(Register_viewer_8), .o_immd_neg(display_registerviewer_8_o_immd_neg),
    .o_immd_dig(display_registerviewer_8_o_immd_dig), .o_immd_dig_1(display_registerviewer_8_o_immd_dig_1),
    .o_immd_dig_2(display_registerviewer_8_o_immd_dig_2),
    .o_immd_dig_3(display_registerviewer_8_o_immd_dig_3), .o_immd_dig_4(display_registerviewer_8_o_immd_dig_4));
  Hex_Digit_Display hex_digit_display_46 (.value(display_registerviewer_8_o_immd_dig_4));  // open: dp
  Hex_Digit_Display hex_digit_display_47 (.value(display_displaysignalgenerator_1_o_rs2_dig));  // open: dp
  new_halt new_halt_1 (
    .halt(MEM_WB_controlunitrelated_6), .clk(new_input_1_clk_2), .latch_wrt(new_halt_1_latch_wrt),
    .pc_enable(new_halt_1_pc_enable));
  new_input new_input_1 (
    .clk(clock_1_out), .buffer(keyboard_1_data), .clear(new_input_1_clear), .clk_2(new_input_1_clk_2));
  Clock clock_1 (.out(clock_1_out));
  _7_Segment_Display u_7_segment_display_9 (.g(display_displaysignalgenerator_1_o_immd_neg));  // open: f, a, b, e, d, c, dp
  Hex_Digit_Display hex_digit_display_48 (.value(display_displaysignalgenerator_1_o_rs2_dig_1));  // open: dp
  Adder adder_1 (.a(PC_q), .b(8'h1), .out(adder_1_out));  // open: cin, cout
  Keyboard #(.buflen(1)) keyboard_1 (.clk(clock_1_out), .data(keyboard_1_data));  // open: re, clr, avail
  Hex_Digit_Display hex_digit_display_49 (.value(display_displaysignalgenerator_1_o_immd_dig));  // open: dp
  Hex_Digit_Display hex_digit_display_50 (.value(display_displaysignalgenerator_1_o_immd_dig_1));  // open: dp
  Register #(.trigger("falling")) PC (
    .D(multiplexer_1_out), .en(new_halt_1_pc_enable), .Q(PC_q), .clk(new_input_1_clk_2),
    .clr(new_input_1_clear));
  Multiplexer #(.width(8), .enable("false")) multiplexer_1 (
    .in0(adder_1_out), .in1(SmartSplitter_immediate), .out(multiplexer_1_out), .sel(Comparator_branch));
  ROM #(.dataWidth(16)) rom_1 (.addr(PC_q), .data(rom_1_data));  // open: sel
  Hex_Digit_Display hex_digit_display_51 (.value(display_displaysignalgenerator_1_o_immd_dig_2));  // open: dp
  Hex_Digit_Display hex_digit_display_52 (.value(display_displaysignalgenerator_1_o_immd_dig_3));  // open: dp
  latch_if_id IF_ID (
    .Instuction(rom_1_data), .Instuction_2(IF_ID_instuction_2), .write_ctrl(new_halt_1_latch_wrt),
    .flush_ctrl(new_input_1_clear), .Instuction_3(IF_ID_instuction_3));
  Hex_Digit_Display hex_digit_display_53 (.value(display_displaysignalgenerator_1_o_immd_dig_4));  // open: dp
  display_displaySignalGenerator display_displaysignalgenerator_2 (
    .o_rs2_mtx(display_displaysignalgenerator_2_o_rs2_mtx),
    .o_rs2_mtx_1(display_displaysignalgenerator_2_o_rs2_mtx_1),
    .o_rs2_mtx_2(display_displaysignalgenerator_2_o_rs2_mtx_2),
    .o_rs2_mtx_3(display_displaysignalgenerator_2_o_rs2_mtx_3),
    .o_rs2_dig(display_displaysignalgenerator_2_o_rs2_dig),
    .o_rs2_dig_1(display_displaysignalgenerator_2_o_rs2_dig_1),
    .o_ins_mtx(display_displaysignalgenerator_2_o_ins_mtx),
    .o_ins_mtx_1(display_displaysignalgenerator_2_o_ins_mtx_1),
    .o_ins_mtx_2(display_displaysignalgenerator_2_o_ins_mtx_2),
    .o_ins_mtx_3(display_displaysignalgenerator_2_o_ins_mtx_3),
    .o_ins_mtx_4(display_displaysignalgenerator_2_o_ins_mtx_4),
    .o_ins_mtx_5(display_displaysignalgenerator_2_o_ins_mtx_5),
    .o_ins_mtx_6(display_displaysignalgenerator_2_o_ins_mtx_6),
    .o_ins_mtx_7(display_displaysignalgenerator_2_o_ins_mtx_7),
    .o_ins_mtx_8(display_displaysignalgenerator_2_o_ins_mtx_8),
    .o_ins_mtx_9(display_displaysignalgenerator_2_o_ins_mtx_9),
    .o_ins_mtx_10(display_displaysignalgenerator_2_o_ins_mtx_10),
    .o_ins_mtx_11(display_displaysignalgenerator_2_o_ins_mtx_11),
    .o_ins_mtx_12(display_displaysignalgenerator_2_o_ins_mtx_12),
    .o_ins_mtx_13(display_displaysignalgenerator_2_o_ins_mtx_13),
    .o_ins_mtx_14(display_displaysignalgenerator_2_o_ins_mtx_14),
    .o_ins_mtx_15(display_displaysignalgenerator_2_o_ins_mtx_15),
    .o_rs1_mtx(display_displaysignalgenerator_2_o_rs1_mtx),
    .o_rs1_mtx_1(display_displaysignalgenerator_2_o_rs1_mtx_1),
    .o_rs1_mtx_2(display_displaysignalgenerator_2_o_rs1_mtx_2),
    .o_rs1_mtx_3(display_displaysignalgenerator_2_o_rs1_mtx_3),
    .o_rs1_dig(display_displaysignalgenerator_2_o_rs1_dig),
    .o_rs1_dig_1(display_displaysignalgenerator_2_o_rs1_dig_1), .i_inst(IF_ID_instuction_3),
    .o_immd_neg(display_displaysignalgenerator_2_o_immd_neg),
    .o_immd_dig(display_displaysignalgenerator_2_o_immd_dig),
    .o_immd_dig_1(display_displaysignalgenerator_2_o_immd_dig_1),
    .o_immd_dig_2(display_displaysignalgenerator_2_o_immd_dig_2),
    .o_immd_dig_3(display_displaysignalgenerator_2_o_immd_dig_3),
    .o_immd_dig_4(display_displaysignalgenerator_2_o_immd_dig_4));
  DotMatrix #(.matrixcols(4), .matrixrows(8)) dotmatrix_7 (
    .col0(display_displaysignalgenerator_2_o_ins_mtx_4), .col1(display_displaysignalgenerator_2_o_ins_mtx_5),
    .col2(display_displaysignalgenerator_2_o_ins_mtx_6), .col3(display_displaysignalgenerator_2_o_ins_mtx_7));
  DotMatrix #(.matrixcols(4), .matrixrows(8)) dotmatrix_8 (
    .col0(display_displaysignalgenerator_2_o_ins_mtx), .col1(display_displaysignalgenerator_2_o_ins_mtx_1),
    .col2(display_displaysignalgenerator_2_o_ins_mtx_2), .col3(display_displaysignalgenerator_2_o_ins_mtx_3));
  new_ctrlUnit CtrlUnit (
    .InstructionNum(SmartSplitter_instrnum), .RegWrite(CtrlUnit_regwrite), .MemToReg(CtrlUnit_memtoreg),
    .MemWrite(CtrlUnit_memwrite), .MemRead(CtrlUnit_memread), .AluBSrc(CtrlUnit_alubsrc), .Led(CtrlUnit_led),
    .Halt(CtrlUnit_halt));
  new_splitter SmartSplitter (
    .Instruction(IF_ID_instuction_2), .Rs(SmartSplitter_rs), .Unsigned(SmartSplitter_unsigned),
    .Immediate(SmartSplitter_immediate), .instrNum(SmartSplitter_instrnum), .Rt(SmartSplitter_rt));  // open: SubOp
  DotMatrix #(.matrixcols(4), .matrixrows(8)) dotmatrix_9 (
    .col0(display_displaysignalgenerator_2_o_ins_mtx_8), .col1(display_displaysignalgenerator_2_o_ins_mtx_9),
    .col2(display_displaysignalgenerator_2_o_ins_mtx_10), .col3(display_displaysignalgenerator_2_o_ins_mtx_11));
  DotMatrix #(.matrixcols(4), .matrixrows(8)) dotmatrix_10 (
    .col0(display_displaysignalgenerator_2_o_ins_mtx_12),
    .col1(display_displaysignalgenerator_2_o_ins_mtx_13),
    .col2(display_displaysignalgenerator_2_o_ins_mtx_14), .col3(display_displaysignalgenerator_2_o_ins_mtx_15));
  new_register Register (
    .ReadRegister1(SmartSplitter_rs), .ReadRegister2(SmartSplitter_rt), .WriteRegister(MEM_WB_rs_2),
    .WriteData(MEM_WB_aluout_2), .Viewer(Register_viewer), .Viewer_2(Register_viewer_2),
    .Viewer_3(Register_viewer_3), .Viewer_4(Register_viewer_4), .Viewer_5(Register_viewer_5),
    .Viewer_6(Register_viewer_6), .Viewer_7(Register_viewer_7), .Viewer_8(Register_viewer_8),
    .ReadData1(Register_readdata1), .ReadData2(Register_readdata2),
    .WriteEnable(MEM_WB_controlunitrelated_4), .Clock(new_input_1_clk_2), .Clear(new_input_1_clear));
  new_widener SignExtender (
    .Imm(SmartSplitter_immediate), .\unsigned (SmartSplitter_unsigned), .ImmExtended(SignExtender_immextended));
  Hex_Digit_Display hex_digit_display_54 (.value(display_displaysignalgenerator_2_o_rs1_dig));  // open: dp
  DotMatrix #(.matrixcols(4), .matrixrows(8)) dotmatrix_11 (
    .col0(display_displaysignalgenerator_2_o_rs1_mtx), .col1(display_displaysignalgenerator_2_o_rs1_mtx_1),
    .col2(display_displaysignalgenerator_2_o_rs1_mtx_2), .col3(display_displaysignalgenerator_2_o_rs1_mtx_3));
  Hex_Digit_Display hex_digit_display_55 (.value(display_displaysignalgenerator_2_o_rs1_dig_1));  // open: dp
  DotMatrix #(.matrixcols(4), .matrixrows(8)) dotmatrix_12 (
    .col0(display_displaysignalgenerator_2_o_rs2_mtx), .col1(display_displaysignalgenerator_2_o_rs2_mtx_1),
    .col2(display_displaysignalgenerator_2_o_rs2_mtx_2), .col3(display_displaysignalgenerator_2_o_rs2_mtx_3));
  Hex_Digit_Display hex_digit_display_56 (.value(display_displaysignalgenerator_2_o_rs2_dig));  // open: dp
  Hex_Digit_Display hex_digit_display_57 (.value(display_displaysignalgenerator_2_o_rs2_dig_1));  // open: dp
  _7_Segment_Display u_7_segment_display_10 (.g(display_displaysignalgenerator_2_o_immd_neg));  // open: f, a, b, e, d, c, dp
  hdu_forward hdu_forward_1 (
    .RegWriteMEM(ID_EX_controlunitrelated_8), .RdMEM(ID_EX_rs_2), .RegWriteWB(EX_MEM_controlunitrelated_7),
    .RdWB(EX_MEM_rs_2), .AluOUTMEM(new_alu_1_out), .AluOUTWB(multiplexer_3_out),
    .ReadData(Register_readdata1), .RsRt(SmartSplitter_rs), .ReadData_2(hdu_forward_1_readdata_2));
  Hex_Digit_Display hex_digit_display_58 (.value(display_displaysignalgenerator_2_o_immd_dig));  // open: dp
  Hex_Digit_Display hex_digit_display_59 (.value(display_displaysignalgenerator_2_o_immd_dig_1));  // open: dp
  latch_id_ex ID_EX (
    .Instruction(IF_ID_instuction_3), .Instruction_2(ID_EX_instruction_2), .flush_ctrl(new_input_1_clear),
    .write_ctrl(new_halt_1_latch_wrt), .ControlUnitRelated(new_nop_1_regwrite_2),
    .ControlUnitRelated_8(ID_EX_controlunitrelated_8), .ControlUnitRelated_2(CtrlUnit_memtoreg),
    .ControlUnitRelated_9(ID_EX_controlunitrelated_9), .ControlUnitRelated_3(CtrlUnit_memwrite),
    .ControlUnitRelated_10(ID_EX_controlunitrelated_10), .ControlUnitRelated_4(CtrlUnit_memread),
    .ControlUnitRelated_11(ID_EX_controlunitrelated_11), .ControlUnitRelated_5(CtrlUnit_alubsrc),
    .ControlUnitRelated_12(ID_EX_controlunitrelated_12), .ControlUnitRelated_6(CtrlUnit_led),
    .ControlUnitRelated_13(ID_EX_controlunitrelated_13), .ControlUnitRelated_7(CtrlUnit_halt),
    .ControlUnitRelated_14(ID_EX_controlunitrelated_14), .InstrNum(SmartSplitter_instrnum),
    .InstrNum_2(ID_EX_instrnum_2), .Rs(SmartSplitter_rs), .Rs_2(ID_EX_rs_2), .Read1(Register_readdata1),
    .Read1_2(ID_EX_read1_2), .SignExtender(SignExtender_immextended), .SignExtender_2(ID_EX_signextender_2),
    .Read2(Register_readdata2), .Read2_2(ID_EX_read2_2), .Rt(SmartSplitter_rt), .Rt_2(ID_EX_rt_2));
  new_nop new_nop_1 (
    .instrNum(SmartSplitter_instrnum), .Rs(SmartSplitter_rs), .Rt(SmartSplitter_rt),
    .RegWrite(CtrlUnit_regwrite), .RegWrite_2(new_nop_1_regwrite_2));
  hdu_comparator Comparator (
    .Number(hdu_forward_1_readdata_2), .Unsigned(SmartSplitter_unsigned), .InstrNum(SmartSplitter_instrnum),
    .Branch(Comparator_branch));
  Hex_Digit_Display hex_digit_display_60 (.value(display_displaysignalgenerator_2_o_immd_dig_2));  // open: dp
  Hex_Digit_Display hex_digit_display_61 (.value(display_displaysignalgenerator_2_o_immd_dig_3));  // open: dp
  Hex_Digit_Display hex_digit_display_62 (.value(display_displaysignalgenerator_2_o_immd_dig_4));  // open: dp
  display_displaySignalGenerator display_displaysignalgenerator_3 (
    .o_rs2_mtx(display_displaysignalgenerator_3_o_rs2_mtx),
    .o_rs2_mtx_1(display_displaysignalgenerator_3_o_rs2_mtx_1),
    .o_rs2_mtx_2(display_displaysignalgenerator_3_o_rs2_mtx_2),
    .o_rs2_mtx_3(display_displaysignalgenerator_3_o_rs2_mtx_3),
    .o_rs2_dig(display_displaysignalgenerator_3_o_rs2_dig),
    .o_rs2_dig_1(display_displaysignalgenerator_3_o_rs2_dig_1),
    .o_ins_mtx(display_displaysignalgenerator_3_o_ins_mtx),
    .o_ins_mtx_1(display_displaysignalgenerator_3_o_ins_mtx_1),
    .o_ins_mtx_2(display_displaysignalgenerator_3_o_ins_mtx_2),
    .o_ins_mtx_3(display_displaysignalgenerator_3_o_ins_mtx_3),
    .o_ins_mtx_4(display_displaysignalgenerator_3_o_ins_mtx_4),
    .o_ins_mtx_5(display_displaysignalgenerator_3_o_ins_mtx_5),
    .o_ins_mtx_6(display_displaysignalgenerator_3_o_ins_mtx_6),
    .o_ins_mtx_7(display_displaysignalgenerator_3_o_ins_mtx_7),
    .o_ins_mtx_8(display_displaysignalgenerator_3_o_ins_mtx_8),
    .o_ins_mtx_9(display_displaysignalgenerator_3_o_ins_mtx_9),
    .o_ins_mtx_10(display_displaysignalgenerator_3_o_ins_mtx_10),
    .o_ins_mtx_11(display_displaysignalgenerator_3_o_ins_mtx_11),
    .o_ins_mtx_12(display_displaysignalgenerator_3_o_ins_mtx_12),
    .o_ins_mtx_13(display_displaysignalgenerator_3_o_ins_mtx_13),
    .o_ins_mtx_14(display_displaysignalgenerator_3_o_ins_mtx_14),
    .o_ins_mtx_15(display_displaysignalgenerator_3_o_ins_mtx_15),
    .o_rs1_mtx(display_displaysignalgenerator_3_o_rs1_mtx),
    .o_rs1_mtx_1(display_displaysignalgenerator_3_o_rs1_mtx_1),
    .o_rs1_mtx_2(display_displaysignalgenerator_3_o_rs1_mtx_2),
    .o_rs1_mtx_3(display_displaysignalgenerator_3_o_rs1_mtx_3),
    .o_rs1_dig(display_displaysignalgenerator_3_o_rs1_dig),
    .o_rs1_dig_1(display_displaysignalgenerator_3_o_rs1_dig_1), .i_inst(ID_EX_instruction_2),
    .o_immd_neg(display_displaysignalgenerator_3_o_immd_neg),
    .o_immd_dig(display_displaysignalgenerator_3_o_immd_dig),
    .o_immd_dig_1(display_displaysignalgenerator_3_o_immd_dig_1),
    .o_immd_dig_2(display_displaysignalgenerator_3_o_immd_dig_2),
    .o_immd_dig_3(display_displaysignalgenerator_3_o_immd_dig_3),
    .o_immd_dig_4(display_displaysignalgenerator_3_o_immd_dig_4));
  DotMatrix #(.matrixcols(4), .matrixrows(8)) dotmatrix_13 (
    .col0(display_displaysignalgenerator_3_o_ins_mtx_4), .col1(display_displaysignalgenerator_3_o_ins_mtx_5),
    .col2(display_displaysignalgenerator_3_o_ins_mtx_6), .col3(display_displaysignalgenerator_3_o_ins_mtx_7));
  DotMatrix #(.matrixcols(4), .matrixrows(8)) dotmatrix_14 (
    .col0(display_displaysignalgenerator_3_o_ins_mtx), .col1(display_displaysignalgenerator_3_o_ins_mtx_1),
    .col2(display_displaysignalgenerator_3_o_ins_mtx_2), .col3(display_displaysignalgenerator_3_o_ins_mtx_3));
  _7_Segment_Display u_7_segment_display_11 (.g(display_registerviewer_9_o_immd_neg));  // open: f, a, b, e, d, c, dp
  Hex_Digit_Display hex_digit_display_63 (.value(display_registerviewer_9_o_immd_dig));  // open: dp
  DotMatrix #(.matrixcols(4), .matrixrows(8)) dotmatrix_15 (
    .col0(display_displaysignalgenerator_3_o_ins_mtx_12),
    .col1(display_displaysignalgenerator_3_o_ins_mtx_13),
    .col2(display_displaysignalgenerator_3_o_ins_mtx_14), .col3(display_displaysignalgenerator_3_o_ins_mtx_15));
  DotMatrix #(.matrixcols(4), .matrixrows(8)) dotmatrix_16 (
    .col0(display_displaysignalgenerator_3_o_ins_mtx_8), .col1(display_displaysignalgenerator_3_o_ins_mtx_9),
    .col2(display_displaysignalgenerator_3_o_ins_mtx_10), .col3(display_displaysignalgenerator_3_o_ins_mtx_11));
  Hex_Digit_Display hex_digit_display_64 (.value(display_registerviewer_9_o_immd_dig_2));  // open: dp
  Hex_Digit_Display hex_digit_display_65 (.value(display_registerviewer_9_o_immd_dig_1));  // open: dp
  hdu_forward ForwardingA_Rs (
    .RegWriteMEM(EX_MEM_controlunitrelated_7), .RdMEM(EX_MEM_rs_2), .RegWriteWB(MEM_WB_controlunitrelated_4),
    .RdWB(MEM_WB_rs_2), .AluOUTMEM(multiplexer_3_out), .AluOUTWB(MEM_WB_aluout_2), .ReadData(ID_EX_read1_2),
    .RsRt(ID_EX_rs_2), .ReadData_2(ForwardingA_Rs_readdata_2));
  Hex_Digit_Display hex_digit_display_66 (.value(display_displaysignalgenerator_3_o_rs1_dig));  // open: dp
  DotMatrix #(.matrixcols(4), .matrixrows(8)) dotmatrix_17 (
    .col0(display_displaysignalgenerator_3_o_rs1_mtx), .col1(display_displaysignalgenerator_3_o_rs1_mtx_1),
    .col2(display_displaysignalgenerator_3_o_rs1_mtx_2), .col3(display_displaysignalgenerator_3_o_rs1_mtx_3));
  display_registerViewer display_registerviewer_9 (
    .in_1(ForwardingA_Rs_readdata_2), .o_immd_neg(display_registerviewer_9_o_immd_neg),
    .o_immd_dig(display_registerviewer_9_o_immd_dig), .o_immd_dig_1(display_registerviewer_9_o_immd_dig_1),
    .o_immd_dig_2(display_registerviewer_9_o_immd_dig_2),
    .o_immd_dig_3(display_registerviewer_9_o_immd_dig_3), .o_immd_dig_4(display_registerviewer_9_o_immd_dig_4));
  Hex_Digit_Display hex_digit_display_67 (.value(display_registerviewer_9_o_immd_dig_4));  // open: dp
  Hex_Digit_Display hex_digit_display_68 (.value(display_registerviewer_9_o_immd_dig_3));  // open: dp
  Hex_Digit_Display hex_digit_display_69 (.value(display_displaysignalgenerator_3_o_rs1_dig_1));  // open: dp
  DotMatrix #(.matrixcols(4), .matrixrows(8)) dotmatrix_18 (
    .col0(display_displaysignalgenerator_3_o_rs2_mtx), .col1(display_displaysignalgenerator_3_o_rs2_mtx_1),
    .col2(display_displaysignalgenerator_3_o_rs2_mtx_2), .col3(display_displaysignalgenerator_3_o_rs2_mtx_3));
  _7_Segment_Display u_7_segment_display_12 (.g(display_registerviewer_10_o_immd_neg));  // open: f, a, b, e, d, c, dp
  Hex_Digit_Display hex_digit_display_70 (.value(display_registerviewer_10_o_immd_dig));  // open: dp
  Hex_Digit_Display hex_digit_display_71 (.value(display_displaysignalgenerator_3_o_rs2_dig));  // open: dp
  Hex_Digit_Display hex_digit_display_72 (.value(display_displaysignalgenerator_3_o_rs2_dig_1));  // open: dp
  Hex_Digit_Display hex_digit_display_73 (.value(display_registerviewer_10_o_immd_dig_1));  // open: dp
  Hex_Digit_Display hex_digit_display_74 (.value(display_registerviewer_10_o_immd_dig_2));  // open: dp
  hdu_forward ForwardingB_Rt (
    .RegWriteMEM(EX_MEM_controlunitrelated_7), .RdMEM(EX_MEM_rs_2), .RegWriteWB(MEM_WB_controlunitrelated_4),
    .RdWB(MEM_WB_rs_2), .AluOUTMEM(multiplexer_3_out), .AluOUTWB(MEM_WB_aluout_2), .ReadData(ID_EX_read2_2),
    .RsRt(ID_EX_rt_2), .ReadData_2(ForwardingB_Rt_readdata_2));
  _7_Segment_Display u_7_segment_display_13 (.g(display_displaysignalgenerator_3_o_immd_neg));  // open: f, a, b, e, d, c, dp
  Hex_Digit_Display hex_digit_display_75 (.value(display_displaysignalgenerator_3_o_immd_dig));  // open: dp
  Hex_Digit_Display hex_digit_display_76 (.value(display_registerviewer_10_o_immd_dig_3));  // open: dp
  Hex_Digit_Display hex_digit_display_77 (.value(display_registerviewer_10_o_immd_dig_4));  // open: dp
  new_alu new_alu_1 (
    .Rd(ForwardingA_Rs_readdata_2), .R_prime_t(multiplexer_2_out), .InstrNum(ID_EX_instrnum_2),
    .Out(new_alu_1_out));
  Multiplexer #(.width(16), .enable("false")) multiplexer_2 (
    .in0(ForwardingB_Rt_readdata_2), .in1(ID_EX_signextender_2), .out(multiplexer_2_out),
    .sel(ID_EX_controlunitrelated_12));
  Hex_Digit_Display hex_digit_display_78 (.value(display_displaysignalgenerator_3_o_immd_dig_2));  // open: dp
  Hex_Digit_Display hex_digit_display_79 (.value(display_displaysignalgenerator_3_o_immd_dig_1));  // open: dp
  _7_Segment_Display u_7_segment_display_14 (.g(display_registerviewer_11_o_immd_neg));  // open: f, a, b, e, d, c, dp
  display_registerViewer display_registerviewer_10 (
    .in_1(multiplexer_2_out), .o_immd_neg(display_registerviewer_10_o_immd_neg),
    .o_immd_dig(display_registerviewer_10_o_immd_dig), .o_immd_dig_1(display_registerviewer_10_o_immd_dig_1),
    .o_immd_dig_2(display_registerviewer_10_o_immd_dig_2),
    .o_immd_dig_3(display_registerviewer_10_o_immd_dig_3),
    .o_immd_dig_4(display_registerviewer_10_o_immd_dig_4));
  latch_ex_mem EX_MEM (
    .flush_ctrl(new_input_1_clear), .write_ctrl(new_halt_1_latch_wrt),
    .ControlUnitRelated(ID_EX_controlunitrelated_8), .ControlUnitRelated_7(EX_MEM_controlunitrelated_7),
    .ControlUnitRelated_2(ID_EX_controlunitrelated_9), .ControlUnitRelated_8(EX_MEM_controlunitrelated_8),
    .ControlUnitRelated_3(ID_EX_controlunitrelated_10), .ControlUnitRelated_9(EX_MEM_controlunitrelated_9),
    .ControlUnitRelated_4(ID_EX_controlunitrelated_11), .ControlUnitRelated_10(EX_MEM_controlunitrelated_10),
    .ControlUnitRelated_5(ID_EX_controlunitrelated_13), .ControlUnitRelated_11(EX_MEM_controlunitrelated_11),
    .ControlUnitRelated_6(ID_EX_controlunitrelated_14), .ControlUnitRelated_12(EX_MEM_controlunitrelated_12),
    .AluOut(new_alu_1_out), .AluOut_2(EX_MEM_aluout_2), .Rs(ID_EX_rs_2), .Rs_2(EX_MEM_rs_2),
    .Instruction(ID_EX_instruction_2), .Instruction_2(EX_MEM_instruction_2),
    .ReadData2(ForwardingA_Rs_readdata_2), .ReadData2_2(EX_MEM_readdata2_2), .Rt(ID_EX_rt_2),
    .Rt_2(EX_MEM_rt_2));
  Hex_Digit_Display hex_digit_display_80 (.value(display_displaysignalgenerator_3_o_immd_dig_4));  // open: dp
  Hex_Digit_Display hex_digit_display_81 (.value(display_displaysignalgenerator_3_o_immd_dig_3));  // open: dp
  Hex_Digit_Display hex_digit_display_82 (.value(display_registerviewer_11_o_immd_dig_1));  // open: dp
  Hex_Digit_Display hex_digit_display_83 (.value(display_registerviewer_11_o_immd_dig));  // open: dp
  Hex_Digit_Display hex_digit_display_84 (.value(display_registerviewer_11_o_immd_dig_3));  // open: dp
  Hex_Digit_Display hex_digit_display_85 (.value(display_registerviewer_11_o_immd_dig_2));  // open: dp
  DotMatrix #(.matrixcols(4), .matrixrows(8)) dotmatrix_19 (
    .col0(display_displaysignalgenerator_4_o_ins_mtx), .col1(display_displaysignalgenerator_4_o_ins_mtx_1),
    .col2(display_displaysignalgenerator_4_o_ins_mtx_2), .col3(display_displaysignalgenerator_4_o_ins_mtx_3));
  display_displaySignalGenerator display_displaysignalgenerator_4 (
    .o_rs2_mtx(display_displaysignalgenerator_4_o_rs2_mtx),
    .o_rs2_mtx_1(display_displaysignalgenerator_4_o_rs2_mtx_1),
    .o_rs2_mtx_2(display_displaysignalgenerator_4_o_rs2_mtx_2),
    .o_rs2_mtx_3(display_displaysignalgenerator_4_o_rs2_mtx_3),
    .o_rs2_dig(display_displaysignalgenerator_4_o_rs2_dig),
    .o_rs2_dig_1(display_displaysignalgenerator_4_o_rs2_dig_1),
    .o_ins_mtx(display_displaysignalgenerator_4_o_ins_mtx),
    .o_ins_mtx_1(display_displaysignalgenerator_4_o_ins_mtx_1),
    .o_ins_mtx_2(display_displaysignalgenerator_4_o_ins_mtx_2),
    .o_ins_mtx_3(display_displaysignalgenerator_4_o_ins_mtx_3),
    .o_ins_mtx_4(display_displaysignalgenerator_4_o_ins_mtx_4),
    .o_ins_mtx_5(display_displaysignalgenerator_4_o_ins_mtx_5),
    .o_ins_mtx_6(display_displaysignalgenerator_4_o_ins_mtx_6),
    .o_ins_mtx_7(display_displaysignalgenerator_4_o_ins_mtx_7),
    .o_ins_mtx_8(display_displaysignalgenerator_4_o_ins_mtx_8),
    .o_ins_mtx_9(display_displaysignalgenerator_4_o_ins_mtx_9),
    .o_ins_mtx_10(display_displaysignalgenerator_4_o_ins_mtx_10),
    .o_ins_mtx_11(display_displaysignalgenerator_4_o_ins_mtx_11),
    .o_ins_mtx_12(display_displaysignalgenerator_4_o_ins_mtx_12),
    .o_ins_mtx_13(display_displaysignalgenerator_4_o_ins_mtx_13),
    .o_ins_mtx_14(display_displaysignalgenerator_4_o_ins_mtx_14),
    .o_ins_mtx_15(display_displaysignalgenerator_4_o_ins_mtx_15),
    .o_rs1_mtx(display_displaysignalgenerator_4_o_rs1_mtx),
    .o_rs1_mtx_1(display_displaysignalgenerator_4_o_rs1_mtx_1),
    .o_rs1_mtx_2(display_displaysignalgenerator_4_o_rs1_mtx_2),
    .o_rs1_mtx_3(display_displaysignalgenerator_4_o_rs1_mtx_3),
    .o_rs1_dig(display_displaysignalgenerator_4_o_rs1_dig),
    .o_rs1_dig_1(display_displaysignalgenerator_4_o_rs1_dig_1), .i_inst(EX_MEM_instruction_2),
    .o_immd_neg(display_displaysignalgenerator_4_o_immd_neg),
    .o_immd_dig(display_displaysignalgenerator_4_o_immd_dig),
    .o_immd_dig_1(display_displaysignalgenerator_4_o_immd_dig_1),
    .o_immd_dig_2(display_displaysignalgenerator_4_o_immd_dig_2),
    .o_immd_dig_3(display_displaysignalgenerator_4_o_immd_dig_3),
    .o_immd_dig_4(display_displaysignalgenerator_4_o_immd_dig_4));
  DotMatrix #(.matrixcols(4), .matrixrows(8)) dotmatrix_20 (
    .col0(display_displaysignalgenerator_4_o_ins_mtx_4), .col1(display_displaysignalgenerator_4_o_ins_mtx_5),
    .col2(display_displaysignalgenerator_4_o_ins_mtx_6), .col3(display_displaysignalgenerator_4_o_ins_mtx_7));
  display_registerViewer display_registerviewer_11 (
    .in_1(new_alu_1_out), .o_immd_neg(display_registerviewer_11_o_immd_neg),
    .o_immd_dig(display_registerviewer_11_o_immd_dig), .o_immd_dig_1(display_registerviewer_11_o_immd_dig_1),
    .o_immd_dig_2(display_registerviewer_11_o_immd_dig_2),
    .o_immd_dig_3(display_registerviewer_11_o_immd_dig_3),
    .o_immd_dig_4(display_registerviewer_11_o_immd_dig_4));
  Hex_Digit_Display hex_digit_display_86 (.value(display_registerviewer_11_o_immd_dig_4));  // open: dp
  DotMatrix #(.matrixcols(4), .matrixrows(8)) dotmatrix_21 (
    .col0(display_displaysignalgenerator_4_o_ins_mtx_8), .col1(display_displaysignalgenerator_4_o_ins_mtx_9),
    .col2(display_displaysignalgenerator_4_o_ins_mtx_10), .col3(display_displaysignalgenerator_4_o_ins_mtx_11));
  DotMatrix #(.matrixcols(4), .matrixrows(8)) dotmatrix_22 (
    .col0(display_displaysignalgenerator_4_o_ins_mtx_12),
    .col1(display_displaysignalgenerator_4_o_ins_mtx_13),
    .col2(display_displaysignalgenerator_4_o_ins_mtx_14), .col3(display_displaysignalgenerator_4_o_ins_mtx_15));
  hdu_forward ForwardingB_Rt_2 (
    .RegWriteMEM(MEM_WB_controlunitrelated_4), .RdMEM(MEM_WB_rs_2), .RegWriteWB(MEM_WB_controlunitrelated_4),
    .RdWB(MEM_WB_rs_2), .AluOUTMEM(MEM_WB_aluout_2), .AluOUTWB(MEM_WB_aluout_2), .ReadData(EX_MEM_aluout_2),
    .RsRt(EX_MEM_rt_2), .ReadData_2(ForwardingB_Rt_2_readdata_2));
  Hex_Digit_Display hex_digit_display_87 (.value(display_displaysignalgenerator_4_o_rs1_dig));  // open: dp
  DotMatrix #(.matrixcols(4), .matrixrows(8)) dotmatrix_23 (
    .col0(display_displaysignalgenerator_4_o_rs1_mtx), .col1(display_displaysignalgenerator_4_o_rs1_mtx_1),
    .col2(display_displaysignalgenerator_4_o_rs1_mtx_2), .col3(display_displaysignalgenerator_4_o_rs1_mtx_3));
  Hex_Digit_Display hex_digit_display_88 (.value(display_displaysignalgenerator_4_o_rs1_dig_1));  // open: dp
  DotMatrix #(.matrixcols(4), .matrixrows(8)) dotmatrix_24 (
    .col0(display_displaysignalgenerator_4_o_rs2_mtx), .col1(display_displaysignalgenerator_4_o_rs2_mtx_1),
    .col2(display_displaysignalgenerator_4_o_rs2_mtx_2), .col3(display_displaysignalgenerator_4_o_rs2_mtx_3));
  hdu_cmux hdu_cmux_1 (
    .WriteData(EX_MEM_readdata2_2), .AluOUTWB(MEM_WB_readdata_2), .WriteData_2(hdu_cmux_1_writedata_2),
    .RegWriteWB(MEM_WB_controlunitrelated_4), .RsWB(MEM_WB_rs_2), .Rt(EX_MEM_rs_2));
  Bit_Extender #(.in_width(16), .out_width(8)) bit_extender_1 (
    .in(ForwardingB_Rt_2_readdata_2), .out(bit_extender_1_out));
  Hex_Digit_Display hex_digit_display_89 (.value(display_displaysignalgenerator_4_o_rs2_dig));  // open: dp
  Hex_Digit_Display hex_digit_display_90 (.value(display_displaysignalgenerator_4_o_rs2_dig_1));  // open: dp
  Multiplexer #(.width(16), .enable("false")) multiplexer_3 (
    .in0(EX_MEM_aluout_2), .in1(ram_1_data), .out(multiplexer_3_out), .sel(EX_MEM_controlunitrelated_8));
  _7_Segment_Display u_7_segment_display_15 (.g(display_displaysignalgenerator_4_o_immd_neg));  // open: f, a, b, e, d, c, dp
  Hex_Digit_Display hex_digit_display_91 (.value(display_displaysignalgenerator_4_o_immd_dig));  // open: dp
  not not_1 (not_1_out, new_input_1_clk_2);
  Hex_Digit_Display hex_digit_display_92 (.value(display_displaysignalgenerator_4_o_immd_dig_1));  // open: dp
  Hex_Digit_Display hex_digit_display_93 (.value(display_displaysignalgenerator_4_o_immd_dig_2));  // open: dp
  latch_mam_wb MEM_WB (
    .flush_ctrl(new_input_1_clear), .write_ctrl(new_halt_1_latch_wrt),
    .ControlUnitRelated(EX_MEM_controlunitrelated_7), .ControlUnitRelated_4(MEM_WB_controlunitrelated_4),
    .ControlUnitRelated_2(EX_MEM_controlunitrelated_11), .ControlUnitRelated_5(MEM_WB_controlunitrelated_5),
    .ControlUnitRelated_3(EX_MEM_controlunitrelated_12), .ControlUnitRelated_6(MEM_WB_controlunitrelated_6),
    .AluOut(multiplexer_3_out), .AluOut_2(MEM_WB_aluout_2), .Rs(EX_MEM_rs_2), .Rs_2(MEM_WB_rs_2),
    .Instruction(EX_MEM_instruction_2), .Instruction_2(MEM_WB_instruction_2), .ReadData(ram_1_data),
    .ReadData_2(MEM_WB_readdata_2));
  RAM #(.dataWidth(16), .bus("separate")) ram_1 (
    .addr(bit_extender_1_out), .din(hdu_cmux_1_writedata_2), .data(ram_1_data),
    .str(EX_MEM_controlunitrelated_9), .sel(1'b1), .clk(not_1_out), .ld(EX_MEM_controlunitrelated_10),
    .clr(new_input_1_clear));
  Hex_Digit_Display hex_digit_display_94 (.value(display_displaysignalgenerator_4_o_immd_dig_3));  // open: dp
  Hex_Digit_Display hex_digit_display_95 (.value(display_displaysignalgenerator_4_o_immd_dig_4));  // open: dp
  DotMatrix #(.matrixcols(4), .matrixrows(8)) dotmatrix_25 (
    .col0(display_displaysignalgenerator_5_o_ins_mtx), .col1(display_displaysignalgenerator_5_o_ins_mtx_1),
    .col2(display_displaysignalgenerator_5_o_ins_mtx_2), .col3(display_displaysignalgenerator_5_o_ins_mtx_3));
  display_displaySignalGenerator display_displaysignalgenerator_5 (
    .o_rs2_mtx(display_displaysignalgenerator_5_o_rs2_mtx),
    .o_rs2_mtx_1(display_displaysignalgenerator_5_o_rs2_mtx_1),
    .o_rs2_mtx_2(display_displaysignalgenerator_5_o_rs2_mtx_2),
    .o_rs2_mtx_3(display_displaysignalgenerator_5_o_rs2_mtx_3),
    .o_rs2_dig(display_displaysignalgenerator_5_o_rs2_dig),
    .o_rs2_dig_1(display_displaysignalgenerator_5_o_rs2_dig_1),
    .o_ins_mtx(display_displaysignalgenerator_5_o_ins_mtx),
    .o_ins_mtx_1(display_displaysignalgenerator_5_o_ins_mtx_1),
    .o_ins_mtx_2(display_displaysignalgenerator_5_o_ins_mtx_2),
    .o_ins_mtx_3(display_displaysignalgenerator_5_o_ins_mtx_3),
    .o_ins_mtx_4(display_displaysignalgenerator_5_o_ins_mtx_4),
    .o_ins_mtx_5(display_displaysignalgenerator_5_o_ins_mtx_5),
    .o_ins_mtx_6(display_displaysignalgenerator_5_o_ins_mtx_6),
    .o_ins_mtx_7(display_displaysignalgenerator_5_o_ins_mtx_7),
    .o_ins_mtx_8(display_displaysignalgenerator_5_o_ins_mtx_8),
    .o_ins_mtx_9(display_displaysignalgenerator_5_o_ins_mtx_9),
    .o_ins_mtx_10(display_displaysignalgenerator_5_o_ins_mtx_10),
    .o_ins_mtx_11(display_displaysignalgenerator_5_o_ins_mtx_11),
    .o_ins_mtx_12(display_displaysignalgenerator_5_o_ins_mtx_12),
    .o_ins_mtx_13(display_displaysignalgenerator_5_o_ins_mtx_13),
    .o_ins_mtx_14(display_displaysignalgenerator_5_o_ins_mtx_14),
    .o_ins_mtx_15(display_displaysignalgenerator_5_o_ins_mtx_15),
    .o_rs1_mtx(display_displaysignalgenerator_5_o_rs1_mtx),
    .o_rs1_mtx_1(display_displaysignalgenerator_5_o_rs1_mtx_1),
    .o_rs1_mtx_2(display_displaysignalgenerator_5_o_rs1_mtx_2),
    .o_rs1_mtx_3(display_displaysignalgenerator_5_o_rs1_mtx_3),
    .o_rs1_dig(display_displaysignalgenerator_5_o_rs1_dig),
    .o_rs1_dig_1(display_displaysignalgenerator_5_o_rs1_dig_1), .i_inst(MEM_WB_instruction_2),
    .o_immd_neg(display_displaysignalgenerator_5_o_immd_neg),
    .o_immd_dig(display_displaysignalgenerator_5_o_immd_dig),
    .o_immd_dig_1(display_displaysignalgenerator_5_o_immd_dig_1),
    .o_immd_dig_2(display_displaysignalgenerator_5_o_immd_dig_2),
    .o_immd_dig_3(display_displaysignalgenerator_5_o_immd_dig_3),
    .o_immd_dig_4(display_displaysignalgenerator_5_o_immd_dig_4));
  Register #(.width(16), .trigger("falling")) register_2 (
    .D(MEM_WB_aluout_2), .en(MEM_WB_controlunitrelated_5), .Q(register_2_q), .clk(new_input_1_clk_2),
    .clr(new_input_1_clear));
  DotMatrix #(.matrixcols(4), .matrixrows(8)) dotmatrix_26 (
    .col0(display_displaysignalgenerator_5_o_ins_mtx_4), .col1(display_displaysignalgenerator_5_o_ins_mtx_5),
    .col2(display_displaysignalgenerator_5_o_ins_mtx_6), .col3(display_displaysignalgenerator_5_o_ins_mtx_7));
  DotMatrix #(.matrixcols(4), .matrixrows(8)) dotmatrix_27 (
    .col0(display_displaysignalgenerator_5_o_ins_mtx_8), .col1(display_displaysignalgenerator_5_o_ins_mtx_9),
    .col2(display_displaysignalgenerator_5_o_ins_mtx_10), .col3(display_displaysignalgenerator_5_o_ins_mtx_11));
  DotMatrix #(.matrixcols(4), .matrixrows(8)) dotmatrix_28 (
    .col0(display_displaysignalgenerator_5_o_ins_mtx_12),
    .col1(display_displaysignalgenerator_5_o_ins_mtx_13),
    .col2(display_displaysignalgenerator_5_o_ins_mtx_14), .col3(display_displaysignalgenerator_5_o_ins_mtx_15));
  DotMatrix #(.matrixcols(4), .matrixrows(8)) dotmatrix_29 (
    .col0(display_displaysignalgenerator_5_o_rs1_mtx), .col1(display_displaysignalgenerator_5_o_rs1_mtx_1),
    .col2(display_displaysignalgenerator_5_o_rs1_mtx_2), .col3(display_displaysignalgenerator_5_o_rs1_mtx_3));
  Hex_Digit_Display hex_digit_display_96 (.value(display_displaysignalgenerator_5_o_rs1_dig));  // open: dp
  Hex_Digit_Display hex_digit_display_97 (.value(display_displaysignalgenerator_5_o_rs1_dig_1));  // open: dp
  DotMatrix #(.matrixcols(4), .matrixrows(8)) dotmatrix_30 (
    .col0(display_displaysignalgenerator_5_o_rs2_mtx), .col1(display_displaysignalgenerator_5_o_rs2_mtx_1),
    .col2(display_displaysignalgenerator_5_o_rs2_mtx_2), .col3(display_displaysignalgenerator_5_o_rs2_mtx_3));
  Hex_Digit_Display hex_digit_display_98 (.value(display_displaysignalgenerator_5_o_rs2_dig_1));  // open: dp
  Hex_Digit_Display hex_digit_display_99 (.value(display_displaysignalgenerator_5_o_rs2_dig));  // open: dp
  _7_Segment_Display u_7_segment_display_16 (.g(display_displaysignalgenerator_5_o_immd_neg));  // open: f, a, b, e, d, c, dp
  Hex_Digit_Display hex_digit_display_100 (.value(display_displaysignalgenerator_5_o_immd_dig));  // open: dp
  Hex_Digit_Display hex_digit_display_101 (.value(display_displaysignalgenerator_5_o_immd_dig_1));  // open: dp
  Hex_Digit_Display hex_digit_display_102 (.value(display_displaysignalgenerator_5_o_immd_dig_2));  // open: dp
  Hex_Digit_Display hex_digit_display_103 (.value(display_displaysignalgenerator_5_o_immd_dig_4));  // open: dp
  Hex_Digit_Display hex_digit_display_104 (.value(display_displaysignalgenerator_5_o_immd_dig_3));  // open: dp

  // Notes on the sheet:
  //   Reg_1
  //   Reg_2
  //   Reg_3
  //   Reg_4
  //   Reg_5
  //   Reg_6
  //   Reg_7
  //   R_0
  //   State_1:Instr_Fetch
  //   Branch
  //   Instuction Rom
  //   contents of rom_1 (hex, n*v repeats v):
  //   1100 130a 150f 170a 1904 1b00 1d04 1f00 0 6700 680 120a 6740 6781 7000
  //   State_2:Instruction_Decode
  //   State_3:Execution
  //   AluBSrc
  //   State_4:Memory
  //   SP 2021 - ECE 1110 - COMPUTER ORGN. AND ARCH.
  //   PROJECT 1 - FIVE STAGES PIPELINING USING LOGISIM
  //   Yinhao Qian & Shaoyu Pei
  //   UPDATED - WB WriteBack Data Fixed
  //   Directions
  //   1. Write assembly codes in ~/decompiler/instr_asm.asm
  //   2. Decompile assembly into machine codes by running ~/decompiler/decompiler.exe
  //   3. Load raw memory data  into instruction memory from ~/decompiler/instr_bin.bin
  //   4. Enable clock ticks and set clock frequency to appropriate value
  //   5. Use hand tool to select the keyboard next to instruction ROM
  //   6. Press 'c' to CLEAR, 'd' to EDGE, Space to CLOCK, 'e' to RUN
  //   Additional Information
  //   1. All memories/registers store values at FALLING EDGE.
  //   2. No stallings are present in this CPU, since all values can be resolved using Forwarding
  //   3. ADD $r0 $r0 is reserved for NOPS operation, no addition will be performed
  //   4. High clock frequency may result in loss of values
  //   State_5:Write_Back
endmodule

module display_displaySignalGenerator (
  input  [15:0] i_inst,
  output [7:0] o_ins_mtx,
  output [7:0] o_ins_mtx_1,
  output [7:0] o_ins_mtx_2,
  output [7:0] o_ins_mtx_3,
  output [7:0] o_ins_mtx_4,
  output [7:0] o_ins_mtx_5,
  output [7:0] o_ins_mtx_6,
  output [7:0] o_ins_mtx_7,
  output [7:0] o_ins_mtx_8,
  output [7:0] o_ins_mtx_9,
  output [7:0] o_ins_mtx_10,
  output [7:0] o_ins_mtx_11,
  output [7:0] o_ins_mtx_12,
  output [7:0] o_ins_mtx_13,
  output [7:0] o_ins_mtx_14,
  output [7:0] o_ins_mtx_15,
  output [7:0] o_rs1_mtx,
  output [7:0] o_rs1_mtx_1,
  output [7:0] o_rs1_mtx_2,
  output [7:0] o_rs1_mtx_3,
  output [3:0] o_rs1_dig,
  output [3:0] o_rs1_dig_1,
  output [7:0] o_rs2_mtx,
  output [7:0] o_rs2_mtx_1,
  output [7:0] o_rs2_mtx_2,
  output [7:0] o_rs2_mtx_3,
  output [3:0] o_rs2_dig,
  output [3:0] o_rs2_dig_1,
  output o_immd_neg,
  output [3:0] o_immd_dig,
  output [3:0] o_immd_dig_1,
  output [3:0] o_immd_dig_2,
  output [3:0] o_immd_dig_3,
  output [3:0] o_immd_dig_4
);

  wire and_1_out, and_3_out, and_5_out, display_determineifrs_1_sig_ifimm, not_1_out, not_3_out, undriven;
  wire [1:0] display_determineifrs_1_sig_rornone;
  wire [2:0] adder_2_out, adder_3_out, adder_11_out, adder_12_out, adder_13_out, adder_14_out,
       bit_extender_4_out, bit_extender_5_out, multiplexer_1_out, multiplexer_2_out, shifter_2_out,
       shifter_3_out;
  wire [3:0] bit_extender_2_out, bit_extender_3_out, divider_1_out, divider_1_rem, divider_2_out,
       divider_2_rem, divider_7_rem;
  wire [4:0] display_instructiondecoder_1_o_instnum;
  wire [6:0] adder_4_out, adder_5_out, adder_6_out, adder_7_out, adder_8_out, adder_9_out, adder_10_out,
       bit_extender_1_out, multiplexer_4_out, not_2_out, shifter_1_out;
  wire [7:0] adder_1_out, divider_3_out, divider_3_rem, divider_4_out, divider_4_rem, divider_5_out,
       divider_5_rem, divider_6_out, divider_6_rem, divider_7_out, multiplexer_3_out;
  wire [7:4] divider_7_rem_2;
  wire [7:7] and_2_out;
  wire [15:0] not_4_out;

  not not_1 (not_1_out, i_inst[8]);
  assign bit_extender_1_out = {{2{1'b0}}, display_instructiondecoder_1_o_instnum};  // Bit_Extender bit_extender_1
  assign bit_extender_2_out = {{1{1'b0}}, i_inst[11:9]};  // Bit_Extender bit_extender_2
  assign bit_extender_3_out = {{1{1'b0}}, i_inst[8:6]};  // Bit_Extender bit_extender_3
  display_determineIfRs display_determineifrs_1 (
    .sig_rOrNone(display_determineifrs_1_sig_rornone), .sig_ifImm(display_determineifrs_1_sig_ifimm),
    .vec_in_instNum(display_instructiondecoder_1_o_instnum));
  assign bit_extender_4_out = {{2{1'b0}}, display_determineifrs_1_sig_rornone[1]};  // Bit_Extender bit_extender_4
  assign bit_extender_5_out = {{2{1'b0}}, display_determineifrs_1_sig_rornone[0]};  // Bit_Extender bit_extender_5
  assign not_2_out = ~i_inst[6:0];  // NOT_Gate not_2, 7 bits wide
  Shifter #(.width(7)) shifter_1 (.in(bit_extender_1_out), .\dist (3'b011), .out(shifter_1_out));
  Divider #(.width(4)) divider_1 (
    .a(bit_extender_2_out), .b(4'b1010), .out(divider_1_out), .rem(divider_1_rem));  // open: upper
  Divider #(.width(4)) divider_2 (
    .a(bit_extender_3_out), .b(4'b1010), .out(divider_2_out), .rem(divider_2_rem));  // open: upper
  Shifter #(.width(3)) shifter_2 (.in(bit_extender_4_out), .\dist (2'b10), .out(shifter_2_out));
  Multiplexer #(.width(3), .enable("false")) multiplexer_1 (
    .in0(shifter_2_out), .in1(3'b000), .out(multiplexer_1_out), .sel(and_5_out));
  Shifter #(.width(3)) shifter_3 (.in(bit_extender_5_out), .\dist (2'b10), .out(shifter_3_out));
  Multiplexer #(.width(3), .enable("false")) multiplexer_2 (
    .in0(shifter_3_out), .in1(3'b000), .out(multiplexer_2_out), .sel(and_5_out));
  Divider divider_3 (.a(multiplexer_3_out), .b(8'ha), .out(divider_3_out), .rem(divider_3_rem));  // open: upper
  and and_1 (and_1_out, not_1_out, i_inst[7]);
  and and_2 (and_2_out[7], i_inst[8], i_inst[7]);
  Adder adder_1 (.a(8'h1), .b({and_2_out[7], not_2_out}), .out(adder_1_out));  // open: cin, cout
  Multiplexer #(.width(8)) multiplexer_3 (
    .in0({and_2_out[7], i_inst[6:0]}), .in1(adder_1_out), .out(multiplexer_3_out), .sel(and_3_out));  // open: en
  and and_3 (and_3_out, and_1_out, not_1_out);
  Divider divider_4 (.a(divider_3_out), .b(8'ha), .out(divider_4_out), .rem(divider_4_rem));  // open: upper
  display_instructionDecoder display_instructiondecoder_1 (
    .i_opcode(i_inst[15:12]), .i_subop(i_inst[0]), .i_unsigned(i_inst[8]),
    .o_instNum(display_instructiondecoder_1_o_instnum));
  Multiplexer #(.width(7), .enable("false")) multiplexer_4 (
    .in0(shifter_1_out), .in1({7{1'b0}}), .out(multiplexer_4_out), .sel(and_5_out));
  Adder #(.width(3)) adder_2 (.a(multiplexer_1_out), .b(3'b001), .out(adder_2_out));  // open: cin, cout
  Adder #(.width(3)) adder_3 (.a(multiplexer_2_out), .b(3'b001), .out(adder_3_out));  // open: cin, cout
  Divider divider_5 (.a(divider_4_out), .b(8'ha), .out(divider_5_out), .rem(divider_5_rem));  // open: upper
  Divider divider_6 (.a(divider_5_out), .b(8'ha), .out(divider_6_out), .rem(divider_6_rem));  // open: upper
  Adder #(.width(7)) adder_4 (.a(multiplexer_4_out), .b(7'b0000001), .out(adder_4_out));  // open: cin, cout
  Adder #(.width(7)) adder_5 (.a(adder_4_out), .b(7'b0000001), .out(adder_5_out));  // open: cin, cout
  Adder #(.width(7)) adder_6 (.a(adder_5_out), .b(7'b0000001), .out(adder_6_out));  // open: cin, cout
  Adder #(.width(7)) adder_7 (.a(adder_6_out), .b(7'b0000001), .out(adder_7_out));  // open: cin, cout
  Adder #(.width(7)) adder_8 (.a(adder_7_out), .b(7'b0000001), .out(adder_8_out));  // open: cin, cout
  Adder #(.width(7)) adder_9 (.a(adder_8_out), .b(7'b0000001), .out(adder_9_out));  // open: cin, cout
  Adder #(.width(7)) adder_10 (.a(adder_9_out), .b(7'b0000001), .out(adder_10_out));  // open: cin, cout
  ROM #(.addrWidth(3)) rom_1 (.addr(multiplexer_1_out), .data(o_rs1_mtx));  // open: sel
  ROM #(.addrWidth(3)) rom_2 (.addr(adder_2_out), .data(o_rs1_mtx_1));  // open: sel
  ROM #(.addrWidth(3)) rom_3 (.addr(multiplexer_2_out), .data(o_rs2_mtx));  // open: sel
  ROM #(.addrWidth(3)) rom_4 (.addr(adder_3_out), .data(o_rs2_mtx_1));  // open: sel
  Divider divider_7 (
    .a(divider_6_out), .b(8'ha), .out(divider_7_out), .rem({divider_7_rem_2, divider_7_rem}));  // open: upper
  Adder #(.width(3)) adder_11 (.a(adder_2_out), .b(3'b001), .out(adder_11_out));  // open: cin, cout
  Adder #(.width(3)) adder_12 (.a(adder_11_out), .b(3'b001), .out(adder_12_out));  // open: cin, cout
  Adder #(.width(3)) adder_13 (.a(adder_3_out), .b(3'b001), .out(adder_13_out));  // open: cin, cout
  Adder #(.width(3)) adder_14 (.a(adder_13_out), .b(3'b001), .out(adder_14_out));  // open: cin, cout
  not not_3 (not_3_out, display_determineifrs_1_sig_ifimm);
  Multiplexer #(.width(4)) multiplexer_5 (
    .in0(4'b0000), .in1(divider_7_out[3:0]), .out(o_immd_dig), .sel(display_determineifrs_1_sig_ifimm));  // open: en
  Multiplexer #(.width(4)) multiplexer_6 (
    .in0(4'b0000), .in1(divider_7_rem), .out(o_immd_dig_1), .sel(display_determineifrs_1_sig_ifimm));  // open: en
  Multiplexer #(.width(4)) multiplexer_7 (
    .in0(4'b0000), .in1(divider_5_rem[3:0]), .out(o_immd_dig_2), .sel(display_determineifrs_1_sig_ifimm));  // open: en
  Multiplexer #(.width(4)) multiplexer_8 (
    .in0(4'b0000), .in1(divider_4_rem[3:0]), .out(o_immd_dig_3), .sel(display_determineifrs_1_sig_ifimm));  // open: en
  Multiplexer #(.width(4)) multiplexer_9 (
    .in0(4'b0000), .in1(divider_3_rem[3:0]), .out(o_immd_dig_4), .sel(display_determineifrs_1_sig_ifimm));  // open: en
  ROM #(.addrWidth(7), .dataWidth(16)) rom_5 (.addr(multiplexer_4_out), .data({o_ins_mtx, o_ins_mtx_1}));  // open: sel
  ROM #(.addrWidth(7), .dataWidth(16)) rom_6 (.addr(adder_4_out), .data({o_ins_mtx_2, o_ins_mtx_3}));  // open: sel
  ROM #(.addrWidth(7), .dataWidth(16)) rom_7 (.addr(adder_5_out), .data({o_ins_mtx_4, o_ins_mtx_5}));  // open: sel
  ROM #(.addrWidth(7), .dataWidth(16)) rom_8 (.addr(adder_6_out), .data({o_ins_mtx_6, o_ins_mtx_7}));  // open: sel
  ROM #(.addrWidth(7), .dataWidth(16)) rom_9 (.addr(adder_7_out), .data({o_ins_mtx_8, o_ins_mtx_9}));  // open: sel
  ROM #(.addrWidth(7), .dataWidth(16)) rom_10 (.addr(adder_8_out), .data({o_ins_mtx_10, o_ins_mtx_11}));  // open: sel
  ROM #(.addrWidth(7), .dataWidth(16)) rom_11 (.addr(adder_9_out), .data({o_ins_mtx_12, o_ins_mtx_13}));  // open: sel
  ROM #(.addrWidth(7), .dataWidth(16)) rom_12 (.addr(adder_10_out), .data({o_ins_mtx_15, o_ins_mtx_14}));  // open: sel
  DotMatrix #(.matrixcols(4), .matrixrows(8)) dotmatrix_1 (
    .col0(o_ins_mtx), .col1(o_ins_mtx_1), .col2(o_ins_mtx_2), .col3(o_ins_mtx_3));
  ROM #(.addrWidth(3)) rom_13 (.addr(adder_11_out), .data(o_rs1_mtx_2));  // open: sel
  ROM #(.addrWidth(3)) rom_14 (.addr(adder_12_out), .data(o_rs1_mtx_3));  // open: sel
  ROM #(.addrWidth(3)) rom_15 (.addr(adder_13_out), .data(o_rs2_mtx_2));  // open: sel
  ROM #(.addrWidth(3)) rom_16 (.addr(adder_14_out), .data(o_rs2_mtx_3));  // open: sel
  and and_4 (o_immd_neg, display_determineifrs_1_sig_ifimm, and_1_out);
  DotMatrix #(.matrixcols(4), .matrixrows(8)) dotmatrix_2 (
    .col0(o_ins_mtx_4), .col1(o_ins_mtx_5), .col2(o_ins_mtx_6), .col3(o_ins_mtx_7));
  DotMatrix #(.matrixcols(4), .matrixrows(8)) dotmatrix_3 (
    .col0(o_ins_mtx_8), .col1(o_ins_mtx_9), .col2(o_ins_mtx_10), .col3(o_ins_mtx_11));
  _7_Segment_Display u_7_segment_display_1 (
    .g(and_1_out), .f(not_3_out), .a(not_3_out), .b(not_3_out), .e(not_3_out), .d(not_3_out), .c(not_3_out));  // open: dp
  Hex_Digit_Display hex_digit_display_1 (.value(o_immd_dig));  // open: dp
  DotMatrix #(.matrixcols(4), .matrixrows(8)) dotmatrix_4 (
    .col0(o_ins_mtx_12), .col1(o_ins_mtx_13), .col2(o_ins_mtx_15), .col3(o_ins_mtx_14));
  Multiplexer #(.width(4)) multiplexer_10 (
    .in0(4'b0000), .in1(divider_1_out), .out(o_rs1_dig), .sel(display_determineifrs_1_sig_rornone[1]));  // open: en
  Multiplexer #(.width(4)) multiplexer_11 (
    .in0(4'b0000), .in1(divider_1_rem), .out(o_rs1_dig_1), .sel(display_determineifrs_1_sig_rornone[1]));  // open: en
  Multiplexer #(.width(4)) multiplexer_12 (
    .in0(4'b0000), .in1(divider_2_out), .out(o_rs2_dig), .sel(display_determineifrs_1_sig_rornone[0]),
    .en(undriven));
  Multiplexer #(.width(4)) multiplexer_13 (
    .in0(4'b0000), .in1(divider_2_rem), .out(o_rs2_dig_1), .sel(display_determineifrs_1_sig_rornone[0]));  // open: en
  Hex_Digit_Display hex_digit_display_2 (.value(o_immd_dig_2));  // open: dp
  Hex_Digit_Display hex_digit_display_3 (.value(o_immd_dig_1));  // open: dp
  Hex_Digit_Display hex_digit_display_4 (.value(o_immd_dig_3));  // open: dp
  Hex_Digit_Display hex_digit_display_5 (.value(o_immd_dig_4));  // open: dp
  DotMatrix #(.matrixcols(4), .matrixrows(8)) dotmatrix_5 (
    .col0(o_rs1_mtx), .col1(o_rs1_mtx_1), .col2(o_rs1_mtx_2), .col3(o_rs1_mtx_3));
  DotMatrix #(.matrixcols(4), .matrixrows(8)) dotmatrix_6 (
    .col0(o_rs2_mtx), .col1(o_rs2_mtx_1), .col2(o_rs2_mtx_2), .col3(o_rs2_mtx_3));
  Hex_Digit_Display hex_digit_display_6 (.value(o_rs1_dig_1));  // open: dp
  Hex_Digit_Display hex_digit_display_7 (.value(o_rs1_dig));  // open: dp
  Hex_Digit_Display hex_digit_display_8 (.value(o_rs2_dig_1));  // open: dp
  Hex_Digit_Display hex_digit_display_9 (.value(o_rs2_dig));  // open: dp
  and and_5 (and_5_out, not_4_out[0], not_4_out[1], not_4_out[2], not_4_out[3], not_4_out[4], not_4_out[5], not_4_out[6], not_4_out[7], not_4_out[8], not_4_out[9], not_4_out[10], not_4_out[11], not_4_out[12], not_4_out[13], not_4_out[14], not_4_out[15]);
  assign not_4_out = ~i_inst;  // NOT_Gate not_4, 16 bits wide

  // Notes on the sheet:
  //   signed
  //   imm
  //   isnegative
  //   contents of rom_1 (hex, n*v repeats v):
  //   4*0 fc a0 b0 ec
  //   contents of rom_2 (hex, n*v repeats v):
  //   4*0 fc a0 b0 ec
  //   contents of rom_3 (hex, n*v repeats v):
  //   4*0 fc a0 b0 ec
  //   contents of rom_4 (hex, n*v repeats v):
  //   4*0 fc a0 b0 ec
  //   contents of rom_5 (hex, n*v repeats v):
  //   4094 b440 6*0 fc90 90fc 1c 1414 fc00 1c14 14fc 0 fc90 90fc 1c 1414 fc00 1c14 14fc 9c fc90 fc00 1c14
  //   fc00 1c14 fc00 1c04 1c9c e4a4 a4bc 1c 404 1c00 fc14 141c 0 fc04 404 1c 41c 41c 0 0 0 e4a4 a4bc 1c
  //   41c 41c 0 0 0 fc20 20fc 5c 5454 7c00 fc00 20fc 2424 84fc a4fc 8c 94a4 c400 0 0 0 84fc a4fc fc a0a0
  //   e000 0 0 0 fca0 a0e0 1c 404 1c00 10fc 1414 0 fca4 a4a4 3c 2020 2000 3c20 2020
  //   contents of rom_6 (hex, n*v repeats v):
  //   4094 b440 6*0 fc90 90fc 1c 1414 fc00 1c14 14fc 0 fc90 90fc 1c 1414 fc00 1c14 14fc 9c fc90 fc00 1c14
  //   fc00 1c14 fc00 1c04 1c9c e4a4 a4bc 1c 404 1c00 fc14 141c 0 fc04 404 1c 41c 41c 0 0 0 e4a4 a4bc 1c
  //   41c 41c 0 0 0 fc20 20fc 5c 5454 7c00 fc00 20fc 2424 84fc a4fc 8c 94a4 c400 0 0 0 84fc a4fc fc a0a0
  //   e000 0 0 0 fca0 a0e0 1c 404 1c00 10fc 1414 0 fca4 a4a4 3c 2020 2000 3c20 2020
  //   contents of rom_7 (hex, n*v repeats v):
  //   4094 b440 6*0 fc90 90fc 1c 1414 fc00 1c14 14fc 0 fc90 90fc 1c 1414 fc00 1c14 14fc 9c fc90 fc00 1c14
  //   fc00 1c14 fc00 1c04 1c9c e4a4 a4bc 1c 404 1c00 fc14 141c 0 fc04 404 1c 41c 41c 0 0 0 e4a4 a4bc 1c
  //   41c 41c 0 0 0 fc20 20fc 5c 5454 7c00 fc00 20fc 2424 84fc a4fc 8c 94a4 c400 0 0 0 84fc a4fc fc a0a0
  //   e000 0 0 0 fca0 a0e0 1c 404 1c00 10fc 1414 0 fca4 a4a4 3c 2020 2000 3c20 2020
  //   contents of rom_8 (hex, n*v repeats v):
  //   4094 b440 6*0 fc90 90fc 1c 1414 fc00 1c14 14fc 0 fc90 90fc 1c 1414 fc00 1c14 14fc 9c fc90 fc00 1c14
  //   fc00 1c14 fc00 1c04 1c9c e4a4 a4bc 1c 404 1c00 fc14 141c 0 fc04 404 1c 41c 41c 0 0 0 e4a4 a4bc 1c
  //   41c 41c 0 0 0 fc20 20fc 5c 5454 7c00 fc00 20fc 2424 84fc a4fc 8c 94a4 c400 0 0 0 84fc a4fc fc a0a0
  //   e000 0 0 0 fca0 a0e0 1c 404 1c00 10fc 1414 0 fca4 a4a4 3c 2020 2000 3c20 2020
  //   contents of rom_9 (hex, n*v repeats v):
  //   4094 b440 6*0 fc90 90fc 1c 1414 fc00 1c14 14fc 0 fc90 90fc 1c 1414 fc00 1c14 14fc 9c fc90 fc00 1c14
  //   fc00 1c14 fc00 1c04 1c9c e4a4 a4bc 1c 404 1c00 fc14 141c 0 fc04 404 1c 41c 41c 0 0 0 e4a4 a4bc 1c
  //   41c 41c 0 0 0 fc20 20fc 5c 5454 7c00 fc00 20fc 2424 84fc a4fc 8c 94a4 c400 0 0 0 84fc a4fc fc a0a0
  //   e000 0 0 0 fca0 a0e0 1c 404 1c00 10fc 1414 0 fca4 a4a4 3c 2020 2000 3c20 2020
  //   contents of rom_10 (hex, n*v repeats v):
  //   4094 b440 6*0 fc90 90fc 1c 1414 fc00 1c14 14fc 0 fc90 90fc 1c 1414 fc00 1c14 14fc 9c fc90 fc00 1c14
  //   fc00 1c14 fc00 1c04 1c9c e4a4 a4bc 1c 404 1c00 fc14 141c 0 fc04 404 1c 41c 41c 0 0 0 e4a4 a4bc 1c
  //   41c 41c 0 0 0 fc20 20fc 5c 5454 7c00 fc00 20fc 2424 84fc a4fc 8c 94a4 c400 0 0 0 84fc a4fc fc a0a0
  //   e000 0 0 0 fca0 a0e0 1c 404 1c00 10fc 1414 0 fca4 a4a4 3c 2020 2000 3c20 2020
  //   contents of rom_11 (hex, n*v repeats v):
  //   4094 b440 6*0 fc90 90fc 1c 1414 fc00 1c14 14fc 0 fc90 90fc 1c 1414 fc00 1c14 14fc 9c fc90 fc00 1c14
  //   fc00 1c14 fc00 1c04 1c9c e4a4 a4bc 1c 404 1c00 fc14 141c 0 fc04 404 1c 41c 41c 0 0 0 e4a4 a4bc 1c
  //   41c 41c 0 0 0 fc20 20fc 5c 5454 7c00 fc00 20fc 2424 84fc a4fc 8c 94a4 c400 0 0 0 84fc a4fc fc a0a0
  //   e000 0 0 0 fca0 a0e0 1c 404 1c00 10fc 1414 0 fca4 a4a4 3c 2020 2000 3c20 2020
  //   contents of rom_12 (hex, n*v repeats v):
  //   4094 b440 6*0 fc90 90fc 1c 1414 fc00 1c14 14fc 0 fc90 90fc 1c 1414 fc00 1c14 14fc 9c fc90 fc00 1c14
  //   fc00 1c14 fc00 1c04 1c9c e4a4 a4bc 1c 404 1c00 fc14 141c 0 fc04 404 1c 41c 41c 0 0 0 e4a4 a4bc 1c
  //   41c 41c 0 0 0 fc20 20fc 5c 5454 7c00 fc00 20fc 2424 84fc a4fc 8c 94a4 c400 0 0 0 84fc a4fc fc a0a0
  //   e000 0 0 0 fca0 a0e0 1c 404 1c00 10fc 1414 0 fca4 a4a4 3c 2020 2000 3c20 2020
  //   contents of rom_13 (hex, n*v repeats v):
  //   4*0 fc a0 b0 ec
  //   contents of rom_14 (hex, n*v repeats v):
  //   4*0 fc a0 b0 ec
  //   contents of rom_15 (hex, n*v repeats v):
  //   4*0 fc a0 b0 ec
  //   contents of rom_16 (hex, n*v repeats v):
  //   4*0 fc a0 b0 ec
endmodule

module display_determineIfRs (
  input  [4:0] vec_in_instNum,
  output [1:0] sig_rOrNone,
  output sig_ifImm
);

  wire nand_1_out, nand_2_out, nand_3_out, nand_4_out, nand_5_out, nand_6_out, nand_7_out, nand_8_out,
       nand_9_out, nand_10_out, nand_11_out, nand_12_out, nand_13_out, nand_14_out, nand_15_out, nand_16_out,
       nand_17_out, nand_18_out, nand_19_out, nand_20_out, nand_21_out, nand_22_out, nand_23_out,
       nand_24_out, nand_25_out, nand_26_out, nand_27_out, nand_28_out, nand_29_out, nand_30_out,
       nand_31_out, nand_32_out, nand_33_out, nand_34_out, nand_35_out, nand_36_out, nand_37_out, nand_38_out;

  nand nand_1 (nand_1_out, 1'b1, vec_in_instNum[4]);
  nand nand_2 (nand_2_out, 1'b1, vec_in_instNum[3]);
  nand nand_3 (nand_3_out, 1'b1, vec_in_instNum[2]);
  nand nand_4 (nand_4_out, 1'b1, vec_in_instNum[1]);
  nand nand_5 (nand_5_out, 1'b1, vec_in_instNum[4]);
  nand nand_6 (nand_6_out, 1'b1, vec_in_instNum[2]);
  nand nand_7 (nand_7_out, 1'b1, vec_in_instNum[1]);
  nand nand_8 (nand_8_out, 1'b1, vec_in_instNum[4]);
  nand nand_9 (nand_9_out, 1'b1, vec_in_instNum[3]);
  nand nand_10 (nand_10_out, 1'b1, vec_in_instNum[2]);
  nand nand_11 (nand_11_out, 1'b1, vec_in_instNum[4]);
  nand nand_12 (nand_12_out, 1'b1, vec_in_instNum[2]);
  nand nand_13 (nand_13_out, 1'b1, vec_in_instNum[0]);
  nand nand_14 (nand_14_out, 1'b1, vec_in_instNum[4]);
  nand nand_15 (nand_15_out, 1'b1, vec_in_instNum[3]);
  nand nand_16 (nand_16_out, 1'b1, vec_in_instNum[1]);
  nand nand_17 (nand_17_out, 1'b1, vec_in_instNum[4]);
  nand nand_18 (nand_18_out, 1'b1, vec_in_instNum[3]);
  nand nand_19 (nand_19_out, 1'b1, vec_in_instNum[0]);
  nand nand_20 (nand_20_out, 1'b1, vec_in_instNum[4]);
  nand nand_21 (nand_21_out, 1'b1, vec_in_instNum[2]);
  nand nand_22 (nand_22_out, 1'b1, vec_in_instNum[1]);
  nand nand_23 (nand_23_out, 1'b1, vec_in_instNum[4]);
  nand nand_24 (nand_24_out, 1'b1, vec_in_instNum[3]);
  nand nand_25 (nand_25_out, 1'b1, vec_in_instNum[1]);
  nand nand_26 (nand_26_out, 1'b1, vec_in_instNum[4]);
  nand nand_27 (nand_27_out, 1'b1, vec_in_instNum[3]);
  nand nand_28 (nand_28_out, 1'b1, vec_in_instNum[0]);
  nand nand_29 (nand_29_out, nand_1_out, nand_2_out, nand_3_out, vec_in_instNum[1]);
  nand nand_30 (nand_30_out, nand_1_out, vec_in_instNum[3], nand_3_out, nand_4_out);
  nand nand_31 (nand_31_out, nand_5_out, nand_6_out, nand_7_out, vec_in_instNum[0]);
  nand nand_32 (nand_32_out, nand_8_out, nand_9_out, nand_10_out, vec_in_instNum[1]);
  nand nand_33 (nand_33_out, nand_11_out, nand_12_out, vec_in_instNum[1], nand_13_out);
  nand nand_34 (nand_34_out, nand_14_out, nand_15_out, vec_in_instNum[2], nand_16_out);
  nand nand_35 (nand_35_out, nand_17_out, nand_18_out, vec_in_instNum[2], nand_19_out);
  nand nand_36 (nand_36_out, nand_20_out, vec_in_instNum[3], nand_21_out, nand_22_out);
  nand nand_37 (nand_37_out, nand_23_out, nand_24_out, nand_25_out, vec_in_instNum[0]);
  nand nand_38 (nand_38_out, nand_26_out, nand_27_out, vec_in_instNum[2], nand_28_out);
  nand nand_39 (sig_ifImm, nand_29_out, nand_30_out);
  nand nand_40 (sig_rOrNone[1], nand_31_out, nand_32_out, nand_33_out, nand_34_out, nand_35_out, nand_36_out);
  nand nand_41 (sig_rOrNone[0], nand_37_out, nand_38_out);
endmodule

module display_instructionDecoder (
  input  [3:0] i_opcode,
  input  i_subop,
  input  i_unsigned,
  output [4:0] o_instNum
);

  wire nand_1_out, nand_2_out, nand_3_out, nand_4_out, nand_5_out, nand_6_out, nand_7_out, nand_8_out,
       nand_9_out, nand_10_out, nand_11_out, nand_12_out, nand_13_out, nand_14_out, nand_15_out, nand_16_out,
       nand_17_out, nand_18_out, nand_19_out, nand_20_out, nand_21_out, nand_22_out, nand_23_out,
       nand_24_out, nand_25_out, nand_26_out, nand_27_out;

  nand nand_1 (nand_1_out, 1'b1, i_opcode[3]);
  nand nand_2 (nand_2_out, 1'b1, i_opcode[2]);
  nand nand_3 (nand_3_out, 1'b1, i_opcode[1]);
  nand nand_4 (nand_4_out, 1'b1, i_opcode[0]);
  nand nand_5 (nand_5_out, 1'b1, i_subop);
  nand nand_6 (nand_6_out, 1'b1, i_opcode[2]);
  nand nand_7 (nand_7_out, 1'b1, i_opcode[0]);
  nand nand_8 (nand_8_out, 1'b1, i_opcode[3]);
  nand nand_9 (nand_9_out, 1'b1, i_opcode[0]);
  nand nand_10 (nand_10_out, 1'b1, i_subop);
  nand nand_11 (nand_11_out, 1'b1, i_opcode[3]);
  nand nand_12 (nand_12_out, 1'b1, i_opcode[0]);
  nand nand_13 (nand_13_out, 1'b1, i_opcode[3]);
  nand nand_14 (nand_14_out, 1'b1, i_subop);
  nand nand_15 (nand_15_out, nand_1_out, nand_2_out, nand_3_out, i_opcode[0]);
  nand nand_16 (nand_16_out, nand_1_out, i_opcode[2], i_opcode[1], nand_4_out, i_subop);
  nand nand_17 (nand_17_out, i_opcode[2], i_opcode[1], i_opcode[0], nand_5_out);
  nand nand_18 (nand_18_out, i_opcode[3], i_opcode[2], i_opcode[1], i_opcode[0]);
  nand nand_19 (nand_19_out, nand_1_out, nand_2_out, nand_3_out, nand_4_out, nand_5_out);
  nand nand_20 (nand_20_out, nand_1_out, nand_2_out, nand_3_out, i_opcode[0], i_unsigned);
  nand nand_21 (nand_21_out, nand_1_out, i_opcode[2], i_opcode[1], nand_5_out);
  nand nand_22 (nand_22_out, i_opcode[3], nand_2_out, i_opcode[1], nand_4_out);
  nand nand_23 (nand_23_out, i_opcode[3], nand_6_out, nand_7_out);
  nand nand_24 (nand_24_out, i_opcode[3], i_opcode[2], i_opcode[1], i_opcode[0]);
  nand nand_25 (nand_25_out, nand_8_out, i_opcode[1], nand_9_out, nand_10_out);
  nand nand_26 (nand_26_out, nand_11_out, i_opcode[2], i_opcode[1], nand_12_out);
  nand nand_27 (nand_27_out, nand_13_out, i_opcode[2], i_opcode[1], nand_14_out);
  nand nand_28 (o_instNum[1], nand_15_out, nand_16_out, nand_17_out, nand_18_out);
  nand nand_29 (o_instNum[0], nand_19_out, nand_20_out, nand_21_out, nand_22_out);
  nand nand_30 (o_instNum[3], nand_23_out, nand_24_out);
  nand nand_31 (o_instNum[2], nand_25_out, nand_26_out, nand_27_out);

  assign o_instNum[4] = 1'b0;
endmodule

module latch_if_id (
  input  flush_ctrl,
  input  write_ctrl,
  input  [15:0] Instuction,
  output [15:0] Instuction_2,
  output [15:0] Instuction_3
);

  Register #(.width(16)) u_Instuction (.D(Instuction), .en(1'b1), .Q(Instuction_2), .clk(write_ctrl), .clr(flush_ctrl));

  assign Instuction_3 = Instuction_2;
endmodule

module latch_id_ex (
  input  flush_ctrl,
  input  write_ctrl,
  input  ControlUnitRelated,
  input  ControlUnitRelated_2,
  input  ControlUnitRelated_3,
  input  ControlUnitRelated_4,
  input  ControlUnitRelated_5,
  input  ControlUnitRelated_6,
  input  ControlUnitRelated_7,
  input  [3:0] InstrNum,
  input  [2:0] Rs,
  input  [2:0] Rt,
  input  [15:0] Read1,
  input  [15:0] Read2,
  input  [15:0] SignExtender,
  input  [15:0] Instruction,
  output ControlUnitRelated_8,
  output ControlUnitRelated_9,
  output ControlUnitRelated_10,
  output ControlUnitRelated_11,
  output ControlUnitRelated_12,
  output ControlUnitRelated_13,
  output ControlUnitRelated_14,
  output [3:0] InstrNum_2,
  output [2:0] Rs_2,
  output [2:0] Rt_2,
  output [15:0] Read1_2,
  output [15:0] Read2_2,
  output [15:0] SignExtender_2,
  output [15:0] Instruction_2
);

  Register #(.width(1)) u_ControlUnitRelated (
    .D(ControlUnitRelated), .en(1'b1), .Q(ControlUnitRelated_8), .clk(write_ctrl), .clr(flush_ctrl));
  Register #(.width(1)) u_ControlUnitRelated_2 (
    .D(ControlUnitRelated_2), .en(1'b1), .Q(ControlUnitRelated_9), .clk(write_ctrl), .clr(flush_ctrl));
  Register #(.width(1)) u_ControlUnitRelated_3 (
    .D(ControlUnitRelated_3), .en(1'b1), .Q(ControlUnitRelated_10), .clk(write_ctrl), .clr(flush_ctrl));
  Register #(.width(1)) u_ControlUnitRelated_4 (
    .D(ControlUnitRelated_4), .en(1'b1), .Q(ControlUnitRelated_11), .clk(write_ctrl), .clr(flush_ctrl));
  Register #(.width(1)) u_ControlUnitRelated_5 (
    .D(ControlUnitRelated_5), .en(1'b1), .Q(ControlUnitRelated_12), .clk(write_ctrl), .clr(flush_ctrl));
  Register #(.width(1)) u_ControlUnitRelated_6 (
    .D(ControlUnitRelated_6), .en(1'b1), .Q(ControlUnitRelated_13), .clk(write_ctrl), .clr(flush_ctrl));
  Register #(.width(1)) u_ControlUnitRelated_7 (
    .D(ControlUnitRelated_7), .en(1'b1), .Q(ControlUnitRelated_14), .clk(write_ctrl), .clr(flush_ctrl));
  Register #(.width(4)) u_InstrNum (.D(InstrNum), .en(1'b1), .Q(InstrNum_2), .clk(write_ctrl), .clr(flush_ctrl));
  Register #(.width(3)) u_Rs (.D(Rs), .en(1'b1), .Q(Rs_2), .clk(write_ctrl), .clr(flush_ctrl));
  Register #(.width(3)) u_Rt (.D(Rt), .en(1'b1), .Q(Rt_2), .clk(write_ctrl), .clr(flush_ctrl));
  Register #(.width(16)) u_Read1 (.D(Read1), .en(1'b1), .Q(Read1_2), .clk(write_ctrl), .clr(flush_ctrl));
  Register #(.width(16)) u_Read2 (.D(Read2), .en(1'b1), .Q(Read2_2), .clk(write_ctrl), .clr(flush_ctrl));
  Register #(.width(16)) u_SignExtender (
    .D(SignExtender), .en(1'b1), .Q(SignExtender_2), .clk(write_ctrl), .clr(flush_ctrl));
  Register #(.width(16)) u_Instruction (
    .D(Instruction), .en(1'b1), .Q(Instruction_2), .clk(write_ctrl), .clr(flush_ctrl));
endmodule

module latch_ex_mem (
  input  flush_ctrl,
  input  write_ctrl,
  input  ControlUnitRelated,
  input  ControlUnitRelated_2,
  input  ControlUnitRelated_3,
  input  ControlUnitRelated_4,
  input  ControlUnitRelated_5,
  input  ControlUnitRelated_6,
  input  [15:0] AluOut,
  input  [2:0] Rs,
  input  [2:0] Rt,
  input  [15:0] ReadData2,
  input  [15:0] Instruction,
  output ControlUnitRelated_7,
  output ControlUnitRelated_8,
  output ControlUnitRelated_9,
  output ControlUnitRelated_10,
  output ControlUnitRelated_11,
  output ControlUnitRelated_12,
  output [15:0] AluOut_2,
  output [2:0] Rs_2,
  output [2:0] Rt_2,
  output [15:0] ReadData2_2,
  output [15:0] Instruction_2
);

  Register #(.width(1)) u_ControlUnitRelated (
    .D(ControlUnitRelated), .en(1'b1), .Q(ControlUnitRelated_7), .clk(write_ctrl), .clr(flush_ctrl));
  Register #(.width(1)) u_ControlUnitRelated_2 (
    .D(ControlUnitRelated_2), .en(1'b1), .Q(ControlUnitRelated_8), .clk(write_ctrl), .clr(flush_ctrl));
  Register #(.width(1)) u_ControlUnitRelated_3 (
    .D(ControlUnitRelated_3), .en(1'b1), .Q(ControlUnitRelated_9), .clk(write_ctrl), .clr(flush_ctrl));
  Register #(.width(1)) u_ControlUnitRelated_4 (
    .D(ControlUnitRelated_4), .en(1'b1), .Q(ControlUnitRelated_10), .clk(write_ctrl), .clr(flush_ctrl));
  Register #(.width(1)) u_ControlUnitRelated_5 (
    .D(ControlUnitRelated_5), .en(1'b1), .Q(ControlUnitRelated_11), .clk(write_ctrl), .clr(flush_ctrl));
  Register #(.width(1)) u_ControlUnitRelated_6 (
    .D(ControlUnitRelated_6), .en(1'b1), .Q(ControlUnitRelated_12), .clk(write_ctrl), .clr(flush_ctrl));
  Register #(.width(16)) u_AluOut (.D(AluOut), .en(1'b1), .Q(AluOut_2), .clk(write_ctrl), .clr(flush_ctrl));
  Register #(.width(3)) Read2 (.D(Rs), .en(1'b1), .Q(Rs_2), .clk(write_ctrl), .clr(flush_ctrl));
  Register #(.width(3)) u_Rt (.D(Rt), .en(1'b1), .Q(Rt_2), .clk(write_ctrl), .clr(flush_ctrl));
  Register #(.width(16)) u_ReadData2 (.D(ReadData2), .en(1'b1), .Q(ReadData2_2), .clk(write_ctrl), .clr(flush_ctrl));
  Register #(.width(16)) u_Instruction (
    .D(Instruction), .en(1'b1), .Q(Instruction_2), .clk(write_ctrl), .clr(flush_ctrl));
endmodule

module new_register (
  input  [2:0] ReadRegister1,
  input  [2:0] ReadRegister2,
  input  [2:0] WriteRegister,
  input  [15:0] WriteData,
  input  WriteEnable,
  input  Clear,
  input  Clock,
  output [15:0] Viewer,
  output [15:0] Viewer_2,
  output [15:0] Viewer_3,
  output [15:0] Viewer_4,
  output [15:0] Viewer_5,
  output [15:0] Viewer_6,
  output [15:0] Viewer_7,
  output [15:0] Viewer_8,
  output [15:0] ReadData1,
  output [15:0] ReadData2
);

  wire decoder_1_out0, decoder_1_out1, decoder_1_out2, decoder_1_out3, decoder_1_out4, decoder_1_out5,
       decoder_1_out6, decoder_1_out7;

  Decoder #(.select(3), .disabled(0)) decoder_1 (
    .out0(decoder_1_out0), .out1(decoder_1_out1), .out2(decoder_1_out2), .out3(decoder_1_out3),
    .out4(decoder_1_out4), .out5(decoder_1_out5), .out6(decoder_1_out6), .out7(decoder_1_out7),
    .sel(WriteRegister), .en(WriteEnable));
  Register #(.width(16), .trigger("falling")) register_1 (
    .D(WriteData), .en(decoder_1_out0), .Q(Viewer), .clk(Clock), .clr(Clear));
  Register #(.width(16), .trigger("falling")) register_2 (
    .D(WriteData), .en(decoder_1_out1), .Q(Viewer_2), .clk(Clock), .clr(Clear));
  Register #(.width(16), .trigger("falling")) register_3 (
    .D(WriteData), .en(decoder_1_out2), .Q(Viewer_3), .clk(Clock), .clr(Clear));
  Register #(.width(16), .trigger("falling")) register_4 (
    .D(WriteData), .en(decoder_1_out3), .Q(Viewer_4), .clk(Clock), .clr(Clear));
  Register #(.width(16), .trigger("falling")) register_5 (
    .D(WriteData), .en(decoder_1_out4), .Q(Viewer_5), .clk(Clock), .clr(Clear));
  Register #(.width(16), .trigger("falling")) register_6 (
    .D(WriteData), .en(decoder_1_out5), .Q(Viewer_6), .clk(Clock), .clr(Clear));
  Register #(.width(16), .trigger("falling")) register_7 (
    .D(WriteData), .en(decoder_1_out6), .Q(Viewer_7), .clk(Clock), .clr(Clear));
  Register #(.width(16), .trigger("falling")) register_8 (
    .D(WriteData), .en(decoder_1_out7), .Q(Viewer_8), .clk(Clock), .clr(Clear));
  Multiplexer #(.select(3), .width(16), .enable("false")) multiplexer_1 (
    .in0(Viewer), .in1(Viewer_2), .in2(Viewer_3), .in3(Viewer_4), .in4(Viewer_5), .in5(Viewer_6),
    .in6(Viewer_7), .in7(Viewer_8), .out(ReadData1), .sel(ReadRegister1));
  Multiplexer #(.select(3), .width(16), .enable("false")) multiplexer_2 (
    .in0(Viewer), .in1(Viewer_2), .in2(Viewer_3), .in3(Viewer_4), .in4(Viewer_5), .in5(Viewer_6),
    .in6(Viewer_7), .in7(Viewer_8), .out(ReadData2), .sel(ReadRegister2));
endmodule

module display_registerViewer (
  input  [15:0] in_1,
  output o_immd_neg,
  output [3:0] o_immd_dig,
  output [3:0] o_immd_dig_1,
  output [3:0] o_immd_dig_2,
  output [3:0] o_immd_dig_3,
  output [3:0] o_immd_dig_4
);

  wire [15:0] adder_1_out, divider_1_out, divider_2_out, divider_3_out, divider_4_out, multiplexer_1_out,
       not_1_out;
  wire [15:4] divider_1_rem, divider_2_rem, divider_3_rem, divider_4_rem, divider_5_rem;

  assign not_1_out = ~{1'b0, in_1[14:0]};  // NOT_Gate not_1, 16 bits wide
  Divider #(.width(16)) divider_1 (
    .a(multiplexer_1_out), .b(16'ha), .out(divider_1_out), .rem({divider_1_rem, o_immd_dig_4}));  // open: upper
  Adder #(.width(16)) adder_1 (.a(16'h1), .b({1'b0, not_1_out[14:0]}), .out(adder_1_out));  // open: cin, cout
  Multiplexer #(.width(16)) multiplexer_1 (
    .in0({1'b0, in_1[14:0]}), .in1(adder_1_out), .out(multiplexer_1_out), .sel(in_1[15]));  // open: en
  Divider #(.width(16)) divider_2 (
    .a(divider_1_out), .b(16'ha), .out(divider_2_out), .rem({divider_2_rem, o_immd_dig_3}));  // open: upper
  Divider #(.width(16)) divider_3 (
    .a(divider_2_out), .b(16'ha), .out(divider_3_out), .rem({divider_3_rem, o_immd_dig_2}));  // open: upper
  Divider #(.width(16)) divider_4 (
    .a(divider_3_out), .b(16'ha), .out(divider_4_out), .rem({divider_4_rem, o_immd_dig_1}));  // open: upper
  Divider #(.width(16)) divider_5 (
    .a(divider_4_out), .b(16'ha), .rem({divider_5_rem, o_immd_dig}));  // open: out, upper
  _7_Segment_Display u_7_segment_display_1 (.g(in_1[15]));  // open: f, a, b, e, d, c, dp
  Hex_Digit_Display hex_digit_display_1 (.value(o_immd_dig));  // open: dp
  Hex_Digit_Display hex_digit_display_2 (.value(o_immd_dig_2));  // open: dp
  Hex_Digit_Display hex_digit_display_3 (.value(o_immd_dig_1));  // open: dp
  Hex_Digit_Display hex_digit_display_4 (.value(o_immd_dig_3));  // open: dp
  Hex_Digit_Display hex_digit_display_5 (.value(o_immd_dig_4));  // open: dp

  assign o_immd_neg = in_1[15];

  // Notes on the sheet:
  //   isnegative
endmodule

module latch_mam_wb (
  input  flush_ctrl,
  input  write_ctrl,
  input  ControlUnitRelated,
  input  ControlUnitRelated_2,
  input  ControlUnitRelated_3,
  input  [15:0] AluOut,
  input  [2:0] Rs,
  input  [15:0] ReadData,
  input  [15:0] Instruction,
  output ControlUnitRelated_4,
  output ControlUnitRelated_5,
  output ControlUnitRelated_6,
  output [15:0] AluOut_2,
  output [2:0] Rs_2,
  output [15:0] ReadData_2,
  output [15:0] Instruction_2
);

  Register #(.width(1)) u_ControlUnitRelated (
    .D(ControlUnitRelated), .en(1'b1), .Q(ControlUnitRelated_4), .clk(write_ctrl), .clr(flush_ctrl));
  Register #(.width(1)) u_ControlUnitRelated_2 (
    .D(ControlUnitRelated_2), .en(1'b1), .Q(ControlUnitRelated_5), .clk(write_ctrl), .clr(flush_ctrl));
  Register #(.width(1)) u_ControlUnitRelated_3 (
    .D(ControlUnitRelated_3), .en(1'b1), .Q(ControlUnitRelated_6), .clk(write_ctrl), .clr(flush_ctrl));
  Register #(.width(16)) u_AluOut (.D(AluOut), .en(1'b1), .Q(AluOut_2), .clk(write_ctrl), .clr(flush_ctrl));
  Register #(.width(3)) Read2 (.D(Rs), .en(1'b1), .Q(Rs_2), .clk(write_ctrl), .clr(flush_ctrl));
  Register #(.width(16)) u_ReadData (.D(ReadData), .en(1'b1), .Q(ReadData_2), .clk(write_ctrl), .clr(flush_ctrl));
  Register #(.width(16)) u_Instruction (
    .D(Instruction), .en(1'b1), .Q(Instruction_2), .clk(write_ctrl), .clr(flush_ctrl));
endmodule

module new_splitter (
  input  [15:0] Instruction,
  output [3:0] instrNum,
  output [2:0] Rs,
  output [2:0] Rt,
  output SubOp,
  output Unsigned,
  output [7:0] Immediate
);

  wire [4:4] display_instructiondecoder_1_o_instnum;

  display_instructionDecoder display_instructiondecoder_1 (
    .i_opcode(Instruction[15:12]), .i_subop(Instruction[0]), .i_unsigned(Instruction[8]),
    .o_instNum({display_instructiondecoder_1_o_instnum[4], instrNum}));

  assign Immediate = Instruction[7:0];
  assign Rs = Instruction[11:9];
  assign Rt = Instruction[8:6];
  assign SubOp = Instruction[0];
  assign Unsigned = Instruction[8];
endmodule
module new_ctrlUnit (
  input  [3:0] InstructionNum,
  output RegWrite,
  output MemToReg,
  output MemWrite,
  output MemRead,
  output AluBSrc,
  output Led,
  output Halt
);

  wire nand_1_out, nand_2_out, nand_3_out, nand_4_out, nand_5_out, nand_6_out, nand_7_out, nand_8_out,
       nand_9_out, nand_10_out, nand_11_out, nand_12_out, nand_13_out, nand_14_out, nand_15_out, nand_16_out,
       nand_17_out, nand_18_out, nand_19_out, nand_20_out, nand_21_out, nand_22_out, nand_23_out,
       nand_24_out, nand_25_out, nand_26_out, nand_27_out, nand_28_out, nand_29_out, nand_30_out,
       nand_31_out, nand_32_out, nand_33_out, nand_34_out, nand_35_out, nand_36_out, nand_37_out,
       nand_38_out, nand_39_out, nand_40_out, nand_41_out, nand_42_out, nand_43_out, nand_44_out,
       nand_45_out, nand_46_out, nand_47_out, nand_48_out, nand_49_out, nand_50_out, nand_51_out,
       nand_52_out, nand_53_out, nand_54_out, nand_55_out, nand_56_out, nand_57_out, nand_58_out,
       nand_59_out, nand_60_out, nand_61_out, nand_62_out, nand_63_out, nand_64_out, nand_65_out,
       nand_66_out, nand_67_out, nand_68_out, nand_69_out, nand_70_out, nand_71_out, nand_72_out,
       nand_73_out, nand_74_out, nand_75_out, nand_76_out, nand_77_out, nand_78_out, nand_79_out,
       nand_80_out, nand_81_out, nand_82_out, nand_83_out, nand_84_out, nand_85_out, nand_86_out,
       nand_87_out, nand_88_out, nand_89_out, nand_90_out, nand_91_out, nand_92_out, nand_93_out,
       nand_94_out, nand_95_out, nand_96_out, nand_97_out, nand_98_out, nand_99_out, nand_100_out,
       nand_101_out, nand_102_out, nand_103_out, nand_104_out, nand_105_out, nand_106_out, nand_107_out,
       nand_108_out, nand_109_out, nand_110_out, nand_111_out, nand_112_out, nand_113_out, nand_114_out,
       nand_115_out, nand_116_out, nand_117_out, nand_118_out, nand_119_out, nand_120_out, nand_121_out,
       nand_122_out, nand_123_out, nand_124_out, nand_125_out, nand_126_out, nand_127_out, nand_128_out,
       nand_129_out, nand_130_out, nand_131_out, nand_132_out, nand_133_out, nand_134_out, nand_135_out,
       nand_136_out, nand_137_out, nand_138_out, nand_139_out, nand_140_out, nand_141_out, nand_142_out,
       nand_143_out, nand_144_out, nand_145_out, nand_146_out, nand_147_out, nand_148_out, nand_149_out,
       nand_150_out, nand_151_out, nand_152_out, nand_153_out, nand_154_out, nand_155_out, nand_156_out,
       nand_157_out, nand_158_out, nand_159_out, nand_160_out, nand_161_out, nand_168_out, nand_169_out;

  nand nand_1 (nand_1_out, 1'b1, InstructionNum[3]);
  nand nand_2 (nand_2_out, 1'b1, InstructionNum[2]);
  nand nand_3 (nand_3_out, 1'b1, InstructionNum[3]);
  nand nand_4 (nand_4_out, 1'b1, InstructionNum[2]);
  nand nand_5 (nand_5_out, 1'b1, InstructionNum[3]);
  nand nand_6 (nand_6_out, 1'b1, InstructionNum[2]);
  nand nand_7 (nand_7_out, 1'b1, InstructionNum[3]);
  nand nand_8 (nand_8_out, 1'b1, InstructionNum[2]);
  nand nand_9 (nand_9_out, 1'b1, InstructionNum[3]);
  nand nand_10 (nand_10_out, 1'b1, InstructionNum[2]);
  nand nand_11 (nand_11_out, 1'b1, InstructionNum[3]);
  nand nand_12 (nand_12_out, 1'b1, InstructionNum[2]);
  nand nand_13 (nand_13_out, 1'b1, InstructionNum[3]);
  nand nand_14 (nand_14_out, 1'b1, InstructionNum[2]);
  nand nand_15 (nand_15_out, 1'b1, InstructionNum[3]);
  nand nand_16 (nand_16_out, 1'b1, InstructionNum[2]);
  nand nand_17 (nand_17_out, 1'b1, InstructionNum[3]);
  nand nand_18 (nand_18_out, 1'b1, InstructionNum[3]);
  nand nand_19 (nand_19_out, 1'b1, InstructionNum[1]);
  nand nand_20 (nand_20_out, 1'b1, InstructionNum[1]);
  nand nand_21 (nand_21_out, 1'b1, InstructionNum[3]);
  nand nand_22 (nand_22_out, 1'b1, InstructionNum[3]);
  nand nand_23 (nand_23_out, 1'b1, InstructionNum[1]);
  nand nand_24 (nand_24_out, 1'b1, InstructionNum[1]);
  nand nand_25 (nand_25_out, 1'b1, InstructionNum[3]);
  nand nand_26 (nand_26_out, 1'b1, InstructionNum[3]);
  nand nand_27 (nand_27_out, 1'b1, InstructionNum[0]);
  nand nand_28 (nand_28_out, 1'b1, InstructionNum[0]);
  nand nand_29 (nand_29_out, 1'b1, InstructionNum[3]);
  nand nand_30 (nand_30_out, 1'b1, InstructionNum[3]);
  nand nand_31 (nand_31_out, 1'b1, InstructionNum[0]);
  nand nand_32 (nand_32_out, 1'b1, InstructionNum[0]);
  nand nand_33 (nand_33_out, 1'b1, InstructionNum[3]);
  nand nand_34 (nand_34_out, 1'b1, InstructionNum[3]);
  nand nand_35 (nand_35_out, 1'b1, InstructionNum[1]);
  nand nand_36 (nand_36_out, 1'b1, InstructionNum[1]);
  nand nand_37 (nand_37_out, 1'b1, InstructionNum[3]);
  nand nand_38 (nand_38_out, 1'b1, InstructionNum[3]);
  nand nand_39 (nand_39_out, 1'b1, InstructionNum[1]);
  nand nand_40 (nand_40_out, 1'b1, InstructionNum[1]);
  nand nand_41 (nand_41_out, 1'b1, InstructionNum[3]);
  nand nand_42 (nand_42_out, 1'b1, InstructionNum[2]);
  nand nand_43 (nand_43_out, 1'b1, InstructionNum[3]);
  nand nand_44 (nand_44_out, 1'b1, InstructionNum[2]);
  nand nand_45 (nand_45_out, 1'b1, InstructionNum[2]);
  nand nand_46 (nand_46_out, 1'b1, InstructionNum[2]);
  nand nand_47 (nand_47_out, 1'b1, InstructionNum[2]);
  nand nand_48 (nand_48_out, 1'b1, InstructionNum[2]);
  nand nand_49 (nand_49_out, 1'b1, InstructionNum[0]);
  nand nand_50 (nand_50_out, 1'b1, InstructionNum[0]);
  nand nand_51 (nand_51_out, 1'b1, InstructionNum[2]);
  nand nand_52 (nand_52_out, 1'b1, InstructionNum[2]);
  nand nand_53 (nand_53_out, 1'b1, InstructionNum[0]);
  nand nand_54 (nand_54_out, 1'b1, InstructionNum[0]);
  nand nand_55 (nand_55_out, 1'b1, InstructionNum[3]);
  nand nand_56 (nand_56_out, 1'b1, InstructionNum[3]);
  nand nand_57 (nand_57_out, 1'b1, InstructionNum[3]);
  nand nand_58 (nand_58_out, 1'b1, InstructionNum[3]);
  nand nand_59 (nand_59_out, nand_1_out, nand_2_out);
  nand nand_60 (nand_60_out, nand_3_out, nand_4_out);
  nand nand_61 (nand_61_out, nand_5_out, nand_6_out);
  nand nand_62 (nand_62_out, nand_7_out, nand_8_out);
  nand nand_63 (nand_63_out, nand_9_out, nand_10_out);
  nand nand_64 (nand_64_out, nand_11_out, nand_12_out);
  nand nand_65 (nand_65_out, nand_13_out, nand_14_out);
  nand nand_66 (nand_66_out, nand_15_out, nand_16_out);
  nand nand_67 (nand_67_out, nand_17_out, InstructionNum[2]);
  nand nand_68 (nand_68_out, nand_18_out, InstructionNum[2]);
  nand nand_69 (nand_69_out, nand_19_out, InstructionNum[0]);
  nand nand_70 (nand_70_out, nand_20_out, InstructionNum[0]);
  nand nand_71 (nand_71_out, nand_21_out, InstructionNum[2]);
  nand nand_72 (nand_72_out, nand_22_out, InstructionNum[2]);
  nand nand_73 (nand_73_out, nand_23_out, InstructionNum[0]);
  nand nand_74 (nand_74_out, nand_24_out, InstructionNum[0]);
  nand nand_75 (nand_75_out, nand_25_out, InstructionNum[2]);
  nand nand_76 (nand_76_out, nand_26_out, InstructionNum[2]);
  nand nand_77 (nand_77_out, InstructionNum[1], nand_27_out);
  nand nand_78 (nand_78_out, InstructionNum[1], nand_28_out);
  nand nand_79 (nand_79_out, nand_29_out, InstructionNum[2]);
  nand nand_80 (nand_80_out, nand_30_out, InstructionNum[2]);
  nand nand_81 (nand_81_out, InstructionNum[1], nand_31_out);
  nand nand_82 (nand_82_out, InstructionNum[1], nand_32_out);
  nand nand_83 (nand_83_out, nand_33_out, InstructionNum[2]);
  nand nand_84 (nand_84_out, nand_34_out, InstructionNum[2]);
  nand nand_85 (nand_85_out, nand_35_out, InstructionNum[0]);
  nand nand_86 (nand_86_out, nand_36_out, InstructionNum[0]);
  nand nand_87 (nand_87_out, nand_37_out, InstructionNum[2]);
  nand nand_88 (nand_88_out, nand_38_out, InstructionNum[2]);
  nand nand_89 (nand_89_out, nand_39_out, InstructionNum[0]);
  nand nand_90 (nand_90_out, nand_40_out, InstructionNum[0]);
  nand nand_91 (nand_91_out, nand_41_out, nand_42_out);
  nand nand_92 (nand_92_out, nand_43_out, nand_44_out);
  nand nand_93 (nand_93_out, InstructionNum[3], nand_45_out);
  nand nand_94 (nand_94_out, InstructionNum[3], nand_46_out);
  nand nand_95 (nand_95_out, InstructionNum[3], nand_47_out);
  nand nand_96 (nand_96_out, InstructionNum[3], nand_48_out);
  nand nand_97 (nand_97_out, InstructionNum[1], nand_49_out);
  nand nand_98 (nand_98_out, InstructionNum[1], nand_50_out);
  nand nand_99 (nand_99_out, InstructionNum[3], nand_51_out);
  nand nand_100 (nand_100_out, InstructionNum[3], nand_52_out);
  nand nand_101 (nand_101_out, InstructionNum[1], nand_53_out);
  nand nand_102 (nand_102_out, InstructionNum[1], nand_54_out);
  nand nand_103 (nand_103_out, nand_55_out, InstructionNum[2]);
  nand nand_104 (nand_104_out, nand_56_out, InstructionNum[2]);
  nand nand_105 (nand_105_out, InstructionNum[1], InstructionNum[0]);
  nand nand_106 (nand_106_out, InstructionNum[1], InstructionNum[0]);
  nand nand_107 (nand_107_out, nand_57_out, InstructionNum[2]);
  nand nand_108 (nand_108_out, nand_58_out, InstructionNum[2]);
  nand nand_109 (nand_109_out, InstructionNum[1], InstructionNum[0]);
  nand nand_110 (nand_110_out, InstructionNum[1], InstructionNum[0]);
  nand nand_111 (nand_111_out, nand_59_out, nand_60_out);
  nand nand_112 (nand_112_out, nand_61_out, nand_62_out);
  nand nand_113 (nand_113_out, nand_63_out, nand_64_out);
  nand nand_114 (nand_114_out, nand_65_out, nand_66_out);
  nand nand_115 (nand_115_out, 1'b1, InstructionNum[3]);
  nand nand_116 (nand_116_out, 1'b1, InstructionNum[3]);
  nand nand_117 (nand_117_out, nand_67_out, nand_68_out);
  nand nand_118 (nand_118_out, nand_69_out, nand_70_out);
  nand nand_119 (nand_119_out, nand_71_out, nand_72_out);
  nand nand_120 (nand_120_out, nand_73_out, nand_74_out);
  nand nand_121 (nand_121_out, nand_75_out, nand_76_out);
  nand nand_122 (nand_122_out, nand_77_out, nand_78_out);
  nand nand_123 (nand_123_out, nand_79_out, nand_80_out);
  nand nand_124 (nand_124_out, nand_81_out, nand_82_out);
  nand nand_125 (nand_125_out, nand_83_out, nand_84_out);
  nand nand_126 (nand_126_out, nand_85_out, nand_86_out);
  nand nand_127 (nand_127_out, nand_87_out, nand_88_out);
  nand nand_128 (nand_128_out, nand_89_out, nand_90_out);
  nand nand_129 (nand_129_out, nand_91_out, nand_92_out);
  nand nand_130 (nand_130_out, nand_93_out, nand_94_out);
  nand nand_131 (nand_131_out, 1'b1, InstructionNum[1]);
  nand nand_132 (nand_132_out, nand_95_out, nand_96_out);
  nand nand_133 (nand_133_out, nand_97_out, nand_98_out);
  nand nand_134 (nand_134_out, nand_99_out, nand_100_out);
  nand nand_135 (nand_135_out, nand_101_out, nand_102_out);
  nand nand_136 (nand_136_out, nand_103_out, nand_104_out);
  nand nand_137 (nand_137_out, nand_105_out, nand_106_out);
  nand nand_138 (nand_138_out, nand_107_out, nand_108_out);
  nand nand_139 (nand_139_out, nand_109_out, nand_110_out);
  nand nand_140 (nand_140_out, nand_111_out, InstructionNum[0]);
  nand nand_141 (nand_141_out, nand_112_out, InstructionNum[1]);
  nand nand_142 (nand_142_out, nand_113_out, InstructionNum[0]);
  nand nand_143 (nand_143_out, nand_114_out, InstructionNum[1]);
  nand nand_144 (nand_144_out, nand_115_out, InstructionNum[2]);
  nand nand_145 (nand_145_out, nand_116_out, InstructionNum[2]);
  nand nand_146 (nand_146_out, nand_117_out, nand_118_out);
  nand nand_147 (nand_147_out, nand_119_out, nand_120_out);
  nand nand_148 (nand_148_out, nand_121_out, nand_122_out);
  nand nand_149 (nand_149_out, nand_123_out, nand_124_out);
  nand nand_150 (nand_150_out, nand_125_out, nand_126_out);
  nand nand_151 (nand_151_out, nand_127_out, nand_128_out);
  nand nand_152 (nand_152_out, nand_129_out, InstructionNum[1]);
  nand nand_153 (nand_153_out, nand_130_out, nand_131_out);
  nand nand_154 (nand_154_out, nand_132_out, nand_133_out);
  nand nand_155 (nand_155_out, nand_134_out, nand_135_out);
  nand nand_156 (nand_156_out, nand_136_out, nand_137_out);
  nand nand_157 (nand_157_out, nand_138_out, nand_139_out);
  nand nand_158 (nand_158_out, nand_140_out, nand_141_out);
  nand nand_159 (nand_159_out, nand_142_out, nand_143_out);
  nand nand_160 (nand_160_out, nand_144_out, nand_145_out);
  nand nand_161 (nand_161_out, 1'b1, InstructionNum[1]);
  nand nand_162 (MemToReg, nand_146_out, nand_147_out);
  nand nand_163 (MemWrite, nand_148_out, nand_149_out);
  nand nand_164 (MemRead, nand_150_out, nand_151_out);
  nand nand_165 (AluBSrc, nand_152_out, nand_153_out);
  nand nand_166 (Led, nand_154_out, nand_155_out);
  nand nand_167 (Halt, nand_156_out, nand_157_out);
  nand nand_168 (nand_168_out, nand_158_out, nand_159_out);
  nand nand_169 (nand_169_out, nand_160_out, nand_161_out);
  nand nand_170 (RegWrite, nand_168_out, nand_169_out);
endmodule

module new_widener (
  input  [7:0] Imm,
  input  \unsigned ,
  output [15:0] ImmExtended
);

  Multiplexer #(.enable("false")) multiplexer_1 (.in0(Imm[7]), .in1(1'b0), .out(ImmExtended[15]), .sel(\unsigned ));

  assign ImmExtended[14:0] = {{7{ImmExtended[15]}}, Imm};
endmodule

module new_alu (
  input  [15:0] Rd,
  input  [15:0] R_prime_t,
  input  [3:0] InstrNum,
  output [15:0] Out
);

  wire nand_1_out, nand_2_out, nand_3_out, nand_4_out, nand_5_out, nand_6_out, nand_7_out, nand_8_out,
       nand_9_out, nand_10_out, nand_11_out, nand_12_out, nand_13_out, nand_14_out, nand_15_out, nand_16_out,
       nand_17_out, nand_18_out, nand_19_out, nand_20_out, nand_21_out, nand_22_out, nand_23_out,
       nand_24_out, nand_25_out, nand_26_out, nand_27_out, nand_28_out, nand_29_out, nand_30_out,
       nand_31_out, nand_32_out, nand_33_out, nand_34_out, nand_35_out, nand_36_out, nand_37_out;
  wire [1:0] nand_38_out;
  wire [15:0] adder_1_out, subtractor_1_out;

  nand nand_1 (nand_1_out, 1'b1, InstrNum[3]);
  nand nand_2 (nand_2_out, 1'b1, InstrNum[2]);
  nand nand_3 (nand_3_out, 1'b1, InstrNum[1]);
  nand nand_4 (nand_4_out, 1'b1, InstrNum[0]);
  Adder #(.width(16)) adder_1 (.a(Rd), .b(R_prime_t), .out(adder_1_out));  // open: cin, cout
  Subtractor #(.width(16)) subtractor_1 (.a(Rd), .b(R_prime_t), .out(subtractor_1_out));  // open: bin, bout
  nand nand_5 (nand_5_out, nand_1_out, InstrNum[2]);
  nand nand_6 (nand_6_out, nand_3_out, InstrNum[0]);
  nand nand_7 (nand_7_out, nand_1_out, InstrNum[2]);
  nand nand_8 (nand_8_out, InstrNum[1], nand_4_out);
  nand nand_9 (nand_9_out, InstrNum[3], nand_2_out);
  nand nand_10 (nand_10_out, InstrNum[3], nand_2_out);
  nand nand_11 (nand_11_out, 1'b1, InstrNum[3]);
  nand nand_12 (nand_12_out, 1'b1, InstrNum[3]);
  nand nand_13 (nand_13_out, 1'b1, InstrNum[3]);
  nand nand_14 (nand_14_out, 1'b1, InstrNum[3]);
  nand nand_15 (nand_15_out, nand_5_out, nand_5_out);
  nand nand_16 (nand_16_out, nand_6_out, nand_6_out);
  nand nand_17 (nand_17_out, nand_7_out, nand_7_out);
  nand nand_18 (nand_18_out, nand_8_out, nand_8_out);
  nand nand_19 (nand_19_out, nand_9_out, nand_9_out);
  nand nand_20 (nand_20_out, nand_10_out, nand_10_out);
  nand nand_21 (nand_21_out, nand_11_out, InstrNum[2]);
  nand nand_22 (nand_22_out, nand_12_out, InstrNum[2]);
  nand nand_23 (nand_23_out, nand_13_out, InstrNum[2]);
  nand nand_24 (nand_24_out, nand_14_out, InstrNum[2]);
  nand nand_25 (nand_25_out, nand_15_out, nand_16_out);
  nand nand_26 (nand_26_out, nand_17_out, nand_18_out);
  nand nand_27 (nand_27_out, nand_19_out, nand_3_out);
  nand nand_28 (nand_28_out, nand_20_out, nand_4_out);
  nand nand_29 (nand_29_out, nand_21_out, nand_22_out);
  nand nand_30 (nand_30_out, 1'b1, InstrNum[1]);
  nand nand_31 (nand_31_out, nand_23_out, nand_24_out);
  nand nand_32 (nand_32_out, nand_25_out, nand_26_out);
  nand nand_33 (nand_33_out, nand_27_out, nand_28_out);
  nand nand_34 (nand_34_out, nand_29_out, nand_30_out);
  nand nand_35 (nand_35_out, nand_31_out, 1'b1);
  Multiplexer #(.select(2), .width(16), .enable("false")) multiplexer_1 (
    .in0(adder_1_out), .in1(subtractor_1_out), .in2(Rd), .in3(R_prime_t), .out(Out), .sel(nand_38_out));
  nand nand_36 (nand_36_out, nand_32_out, nand_32_out);
  nand nand_37 (nand_37_out, nand_33_out, nand_33_out);
  nand nand_38 (nand_38_out[0], nand_34_out, nand_35_out);
  nand nand_39 (nand_38_out[1], nand_36_out, nand_37_out);
endmodule

module hdu_comparator (
  input  [15:0] Number,
  input  [3:0] InstrNum,
  input  Unsigned,
  output Branch
);

  wire nand_1_out, nand_2_out, nand_3_out, nand_4_out, nand_5_out, nand_6_out, nand_7_out, nand_8_out,
       nand_9_out, nand_10_out, nand_11_out, nand_12_out, nand_13_out, nand_14_out, nand_15_out, nand_16_out,
       nand_17_out;
  wire [1:0] comparator_1_gt, comparator_2_gt, multiplexer_1_out;

  Comparator #(.width(16)) comparator_1 (
    .a(Number), .b({16{1'b0}}), .gt(comparator_1_gt[0]), .eq(comparator_1_gt[1]));  // open: lt
  Comparator #(.width(16), .mode("unsigned")) comparator_2 (
    .a(Number), .b({16{1'b0}}), .gt(comparator_2_gt[0]), .eq(comparator_2_gt[1]));  // open: lt
  nand nand_1 (nand_1_out, 1'b1, InstrNum[2]);
  nand nand_2 (nand_2_out, 1'b1, InstrNum[1]);
  nand nand_3 (nand_3_out, 1'b1, InstrNum[0]);
  Multiplexer #(.width(2), .enable("false")) multiplexer_1 (
    .in0(comparator_1_gt), .in1(comparator_2_gt), .out(multiplexer_1_out), .sel(Unsigned));
  nand nand_4 (nand_4_out, InstrNum[3], nand_1_out);
  nand nand_5 (nand_5_out, InstrNum[3], nand_1_out);
  nand nand_6 (nand_6_out, nand_4_out, nand_4_out);
  nand nand_7 (nand_7_out, nand_5_out, nand_5_out);
  nand nand_8 (nand_8_out, nand_6_out, nand_2_out);
  nand nand_9 (nand_9_out, nand_3_out, multiplexer_1_out[1]);
  nand nand_10 (nand_10_out, nand_7_out, nand_2_out);
  nand nand_11 (nand_11_out, InstrNum[0], multiplexer_1_out[0]);
  nand nand_12 (nand_12_out, nand_8_out, nand_8_out);
  nand nand_13 (nand_13_out, nand_9_out, nand_9_out);
  nand nand_14 (nand_14_out, nand_10_out, nand_10_out);
  nand nand_15 (nand_15_out, nand_11_out, nand_11_out);
  nand nand_16 (nand_16_out, nand_12_out, nand_13_out);
  nand nand_17 (nand_17_out, nand_14_out, nand_15_out);
  nand nand_18 (Branch, nand_16_out, nand_17_out);
endmodule

module hdu_forward (
  input  [15:0] ReadData,
  input  [15:0] AluOUTMEM,
  input  [15:0] AluOUTWB,
  input  RegWriteMEM,
  input  [2:0] RdMEM,
  input  RegWriteWB,
  input  [2:0] RdWB,
  input  [2:0] RsRt,
  output [15:0] ReadData_2
);

  wire comparator_1_eq, comparator_2_eq, nand_1_out, nand_2_out, nand_3_out, nand_4_out, nand_5_out,
       nand_6_out, nand_7_out, nand_9_out, nand_10_out;
  wire [1:0] nand_8_out;

  Multiplexer #(.select(2), .width(16), .enable("false")) multiplexer_1 (
    .in0(ReadData), .in1(AluOUTMEM), .in2(AluOUTWB), .in3(ReadData), .out(ReadData_2), .sel(nand_8_out));
  Comparator #(.width(3), .mode("unsigned")) comparator_1 (.a(RdMEM), .b(RsRt), .eq(comparator_1_eq));  // open: gt, lt
  Comparator #(.width(3), .mode("unsigned")) comparator_2 (.a(RdWB), .b(RsRt), .eq(comparator_2_eq));  // open: gt, lt
  nand nand_1 (nand_1_out, 1'b1, RegWriteMEM);
  nand nand_2 (nand_2_out, 1'b1, comparator_1_eq);
  nand nand_3 (nand_3_out, nand_1_out, RegWriteWB);
  nand nand_4 (nand_4_out, RegWriteWB, nand_2_out);
  nand nand_5 (nand_5_out, RegWriteMEM, comparator_1_eq);
  nand nand_6 (nand_6_out, nand_3_out, nand_3_out);
  nand nand_7 (nand_7_out, nand_4_out, nand_4_out);
  nand nand_8 (nand_8_out[0], nand_5_out, nand_5_out);
  nand nand_9 (nand_9_out, nand_6_out, comparator_2_eq);
  nand nand_10 (nand_10_out, nand_7_out, comparator_2_eq);
  nand nand_11 (nand_8_out[1], nand_9_out, nand_10_out);

  // Notes on the sheet:
  //   EX/MEM.RegWrite = true
  //   MEM/WB.RegWrite = true
  //   EX/MEM.Rd = ID/EX.RsRt
  //   MEM/WB.Rd = ID/EX.RsRt
endmodule

module hdu_cmux (
  input  [15:0] WriteData,
  input  [15:0] AluOUTWB,
  input  RegWriteWB,
  input  [2:0] RsWB,
  input  [2:0] Rt,
  output [15:0] WriteData_2
);

  wire and_1_out, comparator_1_eq;

  Comparator #(.width(3), .mode("unsigned")) comparator_1 (.a(RsWB), .b(Rt), .eq(comparator_1_eq));  // open: gt, lt
  and and_1 (and_1_out, RegWriteWB, comparator_1_eq);
  Multiplexer #(.width(16), .enable("false")) multiplexer_1 (
    .in0(WriteData), .in1(AluOUTWB), .out(WriteData_2), .sel(and_1_out));
endmodule

module new_halt (
  input  halt,
  input  clk,
  output latch_wrt,
  output pc_enable
);

  not not_1 (pc_enable, halt);
  and and_1 (latch_wrt, pc_enable, clk);
  // AND_Gate and_2 is placed but not wired

  // Notes on the sheet:
  //   Halt
endmodule

module new_input (
  input  clk,
  input  [6:0] buffer,
  output clear,
  output clk_2
);

  wire and_1_out, comparator_1_eq, comparator_2_eq, comparator_4_eq, t_ff_1_q, t_ff_2_q, xor_1_out;

  T_Flip_Flop t_ff_1 (.clk(clk), .T(comparator_1_eq), .Q(t_ff_1_q), .reset(clear));  // open: Qn, preset, en
  T_Flip_Flop t_ff_2 (.clk(clk), .T(comparator_4_eq), .Q(t_ff_2_q), .reset(clear));  // open: Qn, preset, en
  Comparator #(.width(7), .mode("unsigned")) comparator_1 (
    .a(buffer), .b(7'b1100100), .eq(comparator_1_eq));  // open: gt, lt
  Comparator #(.width(7), .mode("unsigned")) comparator_2 (
    .a(buffer), .b(7'b0100000), .eq(comparator_2_eq));  // open: gt, lt
  Comparator #(.width(7), .mode("unsigned")) comparator_3 (.a(buffer), .b(7'b1100011), .eq(clear));  // open: gt, lt
  Comparator #(.width(7), .mode("unsigned")) comparator_4 (
    .a(buffer), .b(7'b1100101), .eq(comparator_4_eq));  // open: gt, lt
  xor xor_1 (xor_1_out, t_ff_1_q, comparator_2_eq);
  xor xor_2 (clk_2, xor_1_out, and_1_out);
  and and_1 (and_1_out, t_ff_2_q, clk);

  // Notes on the sheet:
  //   Press d to edge
  //   Press c to clear
  //   Press e to run
endmodule

module new_nop (
  input  [3:0] instrNum,
  input  [2:0] Rs,
  input  [2:0] Rt,
  input  RegWrite,
  output RegWrite_2
);

  wire nand_1_out, nand_2_out, nand_3_out, nand_4_out, nand_5_out, nand_6_out, nand_7_out, nand_8_out,
       nand_9_out, nand_10_out, nand_11_out, nand_12_out, nand_13_out, nand_14_out, nand_15_out, nand_16_out,
       nand_17_out, nand_18_out, nand_19_out, nand_20_out, nand_21_out, nand_22_out, nand_23_out,
       nand_24_out, nand_25_out, nand_26_out, nand_27_out;

  nand nand_1 (nand_1_out, 1'b1, instrNum[0]);
  nand nand_2 (nand_2_out, nand_1_out, RegWrite);
  nand nand_3 (nand_3_out, Rt[0], RegWrite);
  nand nand_4 (nand_4_out, Rs[1], RegWrite);
  nand nand_5 (nand_5_out, Rs[2], RegWrite);
  nand nand_6 (nand_6_out, nand_2_out, nand_3_out);
  nand nand_7 (nand_7_out, nand_4_out, nand_5_out);
  nand nand_8 (nand_8_out, nand_6_out, nand_6_out);
  nand nand_9 (nand_9_out, Rt[1], RegWrite);
  nand nand_10 (nand_10_out, Rt[2], RegWrite);
  nand nand_11 (nand_11_out, Rs[0], RegWrite);
  nand nand_12 (nand_12_out, nand_7_out, nand_7_out);
  nand nand_13 (nand_13_out, instrNum[1], RegWrite);
  nand nand_14 (nand_14_out, instrNum[2], RegWrite);
  nand nand_15 (nand_15_out, instrNum[3], RegWrite);
  nand nand_16 (nand_16_out, nand_8_out, nand_9_out);
  nand nand_17 (nand_17_out, nand_10_out, nand_11_out);
  nand nand_18 (nand_18_out, nand_12_out, nand_13_out);
  nand nand_19 (nand_19_out, nand_14_out, nand_15_out);
  nand nand_20 (nand_20_out, nand_16_out, nand_16_out);
  nand nand_21 (nand_21_out, nand_17_out, nand_17_out);
  nand nand_22 (nand_22_out, nand_18_out, nand_18_out);
  nand nand_23 (nand_23_out, nand_19_out, nand_19_out);
  nand nand_24 (nand_24_out, nand_20_out, nand_21_out);
  nand nand_25 (nand_25_out, nand_22_out, nand_23_out);
  nand nand_26 (nand_26_out, nand_24_out, nand_24_out);
  nand nand_27 (nand_27_out, nand_25_out, nand_25_out);
  nand nand_28 (RegWrite_2, nand_26_out, nand_27_out);
endmodule
