// Logisim project piplineRegisters.circ as structural Verilog: 5 circuits, main circuit main
module main (
);

  IF_ID IF_ID ();  // open: PC_in, Instruc_in, clk, PC_out, Instruc_out
  ID_EX ID_EX ();  // open: WB_in, M_in, EX_in, Read1, Read2, Rs1, Rs2, Rd, Imm, clk, WB_out, M_out, EX_out, Read1_out, Read2_out, Rs1_out, Rs2_out, Rd_out, Imm_out
  EX_MEM EX_MEM ();  // open: WB_in, M_in, ALU_in, Mux_in, Rd_in, clk, WB_out, M_out, ALU_out, MUX_out, Rd_out
  MEM_WB MEM_WB ();  // open: DataMem_in, ALU_in, Rd_in, clk, DataMem_out, ALU_out, Rd_out
endmodule

module IF_ID (
  input  [7:0] PC_in,
  input  [15:0] Instruc_in,
  input  clk,
  output [7:0] PC_out,
  output [15:0] Instruc_out
);

  Register PC (.D(PC_in), .en(1'b1), .Q(PC_out), .clk(clk));  // open: clr
  Register #(.width(16)) Instruction (.D(Instruc_in), .en(1'b1), .Q(Instruc_out), .clk(clk));  // open: clr
endmodule

module ID_EX (
  input  WB_in,
  input  M_in,
  input  EX_in,
  input  [2:0] Read1,
  input  [2:0] Read2,
  input  [2:0] Rs1,
  input  [2:0] Rs2,
  input  [2:0] Rd,
  input  [15:0] Imm,
  input  clk,
  output WB_out,
  output M_out,
  output EX_out,
  output [2:0] Read1_out,
  output [2:0] Read2_out,
  output [2:0] Rs1_out,
  output [2:0] Rs2_out,
  output [2:0] Rd_out,
  output [15:0] Imm_out
);

  Register #(.width(1)) WB (.D(WB_in), .en(1'b1), .Q(WB_out), .clk(clk));  // open: clr
  Register #(.width(1)) M (.D(M_in), .en(1'b1), .Q(M_out), .clk(clk));  // open: clr
  Register #(.width(1)) EX (.D(EX_in), .Q(EX_out), .clk(clk));  // open: en, clr
  Register #(.width(3)) Read_Data_1 (.D(Read1), .en(1'b1), .Q(Read1_out), .clk(clk));  // open: clr
  Register #(.width(3)) Read_Data_2 (.D(Read2), .en(1'b1), .Q(Read2_out), .clk(clk));  // open: clr
  Register #(.width(3)) IF_ID_Rs1 (.D(Rs1), .en(1'b1), .Q(Rs1_out), .clk(clk));  // open: clr
  Register #(.width(3)) IF_ID_Rs2 (.D(Rs2), .en(1'b1), .Q(Rs2_out), .clk(clk));  // open: clr
  Register #(.width(3)) IF_ID_Rd (.D(Rd), .en(1'b1), .Q(Rd_out), .clk(clk));  // open: clr
  Register #(.width(16)) Imm_gen (.D(Imm), .en(1'b1), .Q(Imm_out), .clk(clk));  // open: clr
endmodule

module EX_MEM (
  input  WB_in,
  input  M_in,
  input  [15:0] ALU_in,
  input  [15:0] Mux_in,
  input  [2:0] Rd_in,
  input  clk,
  output WB_out,
  output M_out,
  output [15:0] ALU_out,
  output [15:0] MUX_out,
  output [2:0] Rd_out
);

  Register #(.width(1)) WB (.D(WB_in), .en(1'b1), .Q(WB_out), .clk(clk));  // open: clr
  Register #(.width(1)) M (.D(M_in), .en(1'b1), .Q(M_out), .clk(clk));  // open: clr
  Register #(.width(16)) ALU (.D(ALU_in), .en(1'b1), .Q(ALU_out), .clk(clk));  // open: clr
  Register #(.width(16)) MUX (.D(Mux_in), .en(1'b1), .Q(MUX_out), .clk(clk));  // open: clr
  Register #(.width(3)) Rd (.D(Rd_in), .en(1'b1), .Q(Rd_out), .clk(clk));  // open: clr
endmodule

module MEM_WB (
  input  [15:0] DataMem_in,
  input  [15:0] ALU_in,
  input  [2:0] Rd_in,
  input  clk,
  output [15:0] DataMem_out,
  output [15:0] ALU_out,
  output [2:0] Rd_out
);

  Register #(.width(16)) DataMem (.D(DataMem_in), .en(1'b1), .Q(DataMem_out), .clk(clk));  // open: clr
  Register #(.width(16)) ALU (.D(ALU_in), .en(1'b1), .Q(ALU_out), .clk(clk));  // open: clr
  Register #(.width(3)) Rd (.D(Rd_in), .en(1'b1), .Q(Rd_out), .clk(clk));  // open: clr
endmodule
